// Logisim project lab-05 (1).circ as structural Verilog: 1 circuit, main circuit main
module main (
  input  [15:0] in_1,
  input  in_2,
  input  [1:0] in_3,
  input  in_4,
  input  [1:0] in_5,
  input  in_6,
  input  in_7,
  output [15:0] out_8,
  output [15:0] out_9
);

  wire and_1_out, and_2_out, and_3_out, and_4_out, clock_1_out, decoder_1_out0, decoder_1_out1,
       decoder_1_out2, decoder_1_out3;
  wire [15:0] register_1_q, register_2_q, register_3_q, register_4_q;

  Decoder #(.select(2)) decoder_1 (
    .out0(decoder_1_out0), .out1(decoder_1_out1), .out2(decoder_1_out2), .out3(decoder_1_out3), .sel(in_3),
    .en(in_2));
  and and_1 (and_1_out, decoder_1_out0, in_6);
  and and_2 (and_2_out, decoder_1_out1, in_6);
  and and_3 (and_3_out, decoder_1_out2, in_6);
  and and_4 (and_4_out, decoder_1_out3, in_6);
  Clock clock_1 (.out(clock_1_out));
  Register #(.width(16)) register_1 (.D(in_1), .en(and_1_out), .Q(register_1_q), .clk(clock_1_out), .clr(in_7));
  Register #(.width(16)) register_2 (.D(in_1), .en(and_2_out), .Q(register_2_q), .clk(clock_1_out), .clr(in_7));
  Register #(.width(16)) register_3 (.D(in_1), .en(and_3_out), .Q(register_3_q), .clk(clock_1_out), .clr(in_7));
  Register #(.width(16)) register_4 (.D(in_1), .en(and_4_out), .Q(register_4_q), .clk(clock_1_out), .clr(in_7));
  Multiplexer #(.select(2), .width(16)) multiplexer_1 (
    .in0(register_1_q), .in1(register_2_q), .in2(register_3_q), .in3(register_4_q), .out(out_8), .sel(in_5),
    .en(in_4));
  Multiplexer #(.select(2), .width(16)) multiplexer_2 (
    .in0(register_1_q), .in1(register_2_q), .in2(register_3_q), .in3(register_4_q), .out(out_9), .sel(in_5),
    .en(in_4));
endmodule
