// Logisim project lab 5 Raisa Version.circ as structural Verilog
module main (
  input  [15:0] Data_In,
  input  [15:0] Data_Out_1,
  input  [3:0] Read_Address_1__rs,
  input  [3:0] Read_Address_2__rt,
  input  [15:0] Data_Out_2,
  input  [3:0] Write_Address__rd,
  input  RegWrite
);

  wire CLK_out;

  Register_File register_file_1 (
    .Data_In(Data_In), .Data_Out_1(Data_Out_1), .Read_Address_1_rs(Read_Address_1__rs),
    .Data_Out_2(Data_Out_2), .Read_Address_2_rt(Read_Address_2__rt), .Write_Address__rd(Write_Address__rd),
    .CLK(CLK_out), .Reg_Write(RegWrite));
  Clock CLK (.out(CLK_out));
endmodule

module Register_File (
  input  [15:0] Data_In,
  input  Reg_Write,
  input  [3:0] Read_Address_1_rs,
  input  [3:0] Write_Address__rd,
  input  [3:0] Read_Address_2_rt,
  input  CLK,
  output [15:0] Data_Out_1,
  output [15:0] Data_Out_2
);

  wire and_1_out, decoder_1_out0, decoder_1_out1, decoder_1_out2, decoder_1_out3, decoder_1_out4,
       decoder_1_out5, decoder_1_out6, decoder_1_out7, decoder_1_out8, decoder_1_out9, decoder_1_out10,
       decoder_1_out11, decoder_1_out12, decoder_1_out13, decoder_1_out14, decoder_1_out15;
  wire [15:0] _1_q, _2_q, _3_q, _4_q, _5_q, _6_q, _7_q, _8_q, _9_q, _10_q, _11_q, _12_q, _13_q, _14_q, _15_q,
       _16_q;

  Decoder #(.select(4)) decoder_1 (
    .out0(decoder_1_out0), .out1(decoder_1_out1), .out2(decoder_1_out2), .out3(decoder_1_out3),
    .out4(decoder_1_out4), .out5(decoder_1_out5), .out6(decoder_1_out6), .out7(decoder_1_out7),
    .out8(decoder_1_out8), .out9(decoder_1_out9), .out10(decoder_1_out10), .out11(decoder_1_out11),
    .out12(decoder_1_out12), .out13(decoder_1_out13), .out14(decoder_1_out14), .out15(decoder_1_out15),
    .sel(Write_Address__rd));  // open: en
  and and_1 (and_1_out, decoder_1_out0, Reg_Write);
  Register #(.width(16)) _1 (.D(Data_In), .en(and_1_out), .Q(_1_q), .clk(CLK));  // open: clr
  Register #(.width(16)) _2 (.D(Data_In), .en(decoder_1_out1), .Q(_2_q), .clk(CLK));  // open: clr
  Register #(.width(16)) _3 (.D(Data_In), .en(decoder_1_out2), .Q(_3_q), .clk(CLK));  // open: clr
  Register #(.width(16)) _4 (.D(Data_In), .en(decoder_1_out3), .Q(_4_q), .clk(CLK));  // open: clr
  Register #(.width(16)) _5 (.D(Data_In), .en(decoder_1_out4), .Q(_5_q), .clk(CLK));  // open: clr
  Register #(.width(16)) _6 (.D(Data_In), .en(decoder_1_out5), .Q(_6_q), .clk(CLK));  // open: clr
  Register #(.width(16)) _7 (.D(Data_In), .en(decoder_1_out6), .Q(_7_q), .clk(CLK));  // open: clr
  Register #(.width(16)) _8 (.D(Data_In), .en(decoder_1_out7), .Q(_8_q), .clk(CLK));  // open: clr
  Register #(.width(16)) _9 (.D(Data_In), .en(decoder_1_out8), .Q(_9_q), .clk(CLK));  // open: clr
  Register #(.width(16)) _10 (.D(Data_In), .en(decoder_1_out9), .Q(_10_q), .clk(CLK));  // open: clr
  Register #(.width(16)) _11 (.D(Data_In), .en(decoder_1_out10), .Q(_11_q), .clk(CLK));  // open: clr
  Register #(.width(16)) _12 (.D(Data_In), .en(decoder_1_out11), .Q(_12_q), .clk(CLK));  // open: clr
  Register #(.width(16)) _13 (.D(Data_In), .en(decoder_1_out12), .Q(_13_q), .clk(CLK));  // open: clr
  Register #(.width(16)) _14 (.D(Data_In), .en(decoder_1_out13), .Q(_14_q), .clk(CLK));  // open: clr
  Register #(.width(16)) _15 (.D(Data_In), .en(decoder_1_out14), .Q(_15_q), .clk(CLK));  // open: clr
  Register #(.width(16)) _16 (.D(Data_In), .en(decoder_1_out15), .Q(_16_q), .clk(CLK));  // open: clr
  Multiplexer #(.select(4), .width(16)) multiplexer_1 (
    .in0(_1_q), .in1(_2_q), .in2(_3_q), .in3(_4_q), .in4(_5_q), .in5(_6_q), .in6(_7_q), .in7(_8_q),
    .in8(_9_q), .in9(_10_q), .in10(_11_q), .in11(_12_q), .in12(_13_q), .in13(_14_q), .in14(_15_q),
    .in15(_16_q), .out(Data_Out_1), .sel(Read_Address_1_rs));  // open: en
  Multiplexer #(.select(4), .width(16)) multiplexer_2 (
    .in0(_1_q), .in1(_2_q), .in2(_3_q), .in3(_4_q), .in4(_5_q), .in5(_6_q), .in6(_7_q), .in7(_8_q),
    .in8(_9_q), .in9(_10_q), .in10(_11_q), .in11(_12_q), .in12(_13_q), .in13(_14_q), .in14(_15_q),
    .in15(_16_q), .out(Data_Out_2), .sel(Read_Address_2_rt));  // open: en
endmodule
