// Logisim project lab 6.circ as structural Verilog: 3 circuits, main circuit main
module main (
  input  [15:0] in_1,
  input  [15:0] in_2,
  output [15:0] out_3
);

  _16_BIT_ALU u_16_bit_alu_1 (
    .Result(out_3), .A(in_1), .B(in_2));  // open: Bin, Operation, Overflow_Flag, Cout, Operaton_Flag, Cin
endmodule

// ALU (16 BIT)
module _16_BIT_ALU (
  input  Cin,
  input  [15:0] A,
  input  [15:0] B,
  input  Bin,
  input  [1:0] Operation,
  output [15:0] Result,
  output Overflow_Flag,
  output Cout,
  output Operaton_Flag
);

  wire ALU_1_cout, ALU_2_cout, ALU_3_cout, ALU_4_cout, ALU_5_cout, ALU_6_cout, ALU_7_cout, ALU_8_cout,
       ALU_9_cout, ALU_10_cout, ALU_11_cout, ALU_12_cout, ALU_13_cout, ALU_14_cout;

  _1_BIT_ALU ALU_0 (
    .A(A[0]), .B(B[0]), .Cin(Cin), .Bin(Bin), .Result_0(Result[0]), .Operation(Operation), .Cout(Result[1]));
  _1_BIT_ALU ALU_1 (
    .A(A[1]), .B(B[1]), .Cin(Result[1]), .Bin(Bin), .Result_0(Result[1]), .Operation(Operation),
    .Cout(ALU_1_cout));
  _1_BIT_ALU ALU_2 (
    .A(A[2]), .B(B[2]), .Cin(ALU_1_cout), .Bin(Bin), .Result_0(Result[2]), .Operation(Operation),
    .Cout(ALU_2_cout));
  _1_BIT_ALU ALU_3 (
    .A(A[3]), .B(B[3]), .Cin(ALU_2_cout), .Bin(Bin), .Result_0(Result[3]), .Operation(Operation),
    .Cout(ALU_3_cout));
  _1_BIT_ALU ALU_4 (
    .A(A[4]), .B(B[4]), .Cin(ALU_3_cout), .Bin(Bin), .Result_0(Result[4]), .Operation(Operation),
    .Cout(ALU_4_cout));
  _1_BIT_ALU ALU_5 (
    .A(A[5]), .B(B[5]), .Cin(ALU_4_cout), .Bin(Bin), .Result_0(Result[5]), .Operation(Operation),
    .Cout(ALU_5_cout));
  _1_BIT_ALU ALU_6 (
    .A(A[6]), .B(B[6]), .Cin(ALU_5_cout), .Bin(Bin), .Result_0(Result[6]), .Operation(Operation),
    .Cout(ALU_6_cout));
  _1_BIT_ALU ALU_7 (
    .A(A[7]), .B(B[7]), .Cin(ALU_6_cout), .Bin(Bin), .Result_0(Result[7]), .Operation(Operation),
    .Cout(ALU_7_cout));
  _1_BIT_ALU ALU_8 (
    .A(A[8]), .B(B[8]), .Cin(ALU_7_cout), .Bin(Bin), .Result_0(Result[8]), .Operation(Operation),
    .Cout(ALU_8_cout));
  _1_BIT_ALU ALU_9 (
    .A(A[9]), .B(B[9]), .Cin(ALU_8_cout), .Bin(Bin), .Result_0(Result[9]), .Operation(Operation),
    .Cout(ALU_9_cout));
  _1_BIT_ALU ALU_10 (
    .A(A[10]), .B(B[10]), .Cin(ALU_9_cout), .Bin(Bin), .Result_0(Result[10]), .Operation(Operation),
    .Cout(ALU_10_cout));
  _1_BIT_ALU ALU_11 (
    .A(A[11]), .B(B[11]), .Cin(ALU_10_cout), .Bin(Bin), .Result_0(Result[11]), .Operation(Operation),
    .Cout(ALU_11_cout));
  _1_BIT_ALU ALU_12 (
    .A(A[12]), .B(B[12]), .Cin(ALU_11_cout), .Bin(Bin), .Result_0(Result[12]), .Operation(Operation),
    .Cout(ALU_12_cout));
  _1_BIT_ALU ALU_13 (
    .A(A[13]), .B(B[13]), .Cin(ALU_12_cout), .Bin(Bin), .Result_0(Result[13]), .Operation(Operation),
    .Cout(ALU_13_cout));
  _1_BIT_ALU ALU_14 (
    .A(A[14]), .B(B[14]), .Cin(ALU_13_cout), .Bin(Bin), .Result_0(Result[14]), .Operation(Operation),
    .Cout(ALU_14_cout));
  _1_BIT_ALU ALU_15 (
    .A(A[15]), .B(B[15]), .Cin(ALU_14_cout), .Bin(Bin), .Result_0(Result[15]), .Operation(Operation),
    .Cout(Cout));
  xor xor_1 (Operaton_Flag, Cout, ALU_14_cout);
  nor nor_1 (Overflow_Flag, Result[0], Result[1], Result[2], Result[3], Result[4], Result[5], Result[6], Result[7], Result[8], Result[9], Result[10], Result[11], Result[12], Result[13], Result[14], Result[15]);
endmodule

// ALU 1 BIT
module _1_BIT_ALU (
  input  Cin,
  input  A,
  input  B,
  input  Bin,
  input  [1:0] Operation,
  output Result_0,
  output Cout
);

  wire adder_1_out, and_1_out, multiplexer_1_out, not_1_out, or_1_out;

  not not_1 (not_1_out, B);
  Multiplexer multiplexer_1 (.in0(B), .in1(not_1_out), .out(multiplexer_1_out), .sel(Bin));  // open: en
  and and_1 (and_1_out, A, B);
  or or_1 (or_1_out, A, B);
  Adder #(.width(1)) adder_1 (.a(A), .b(multiplexer_1_out), .out(adder_1_out), .cin(Cin), .cout(Cout));
  Multiplexer #(.select(2)) multiplexer_2 (
    .in0(and_1_out), .in1(or_1_out), .in2(adder_1_out), .out(Result_0), .sel(Operation));  // open: in3, en
endmodule
