// Logisim project 16 Bit ALU.circ as structural Verilog
module _1_Bit_ALU (
  input  in_1,
  input  in_2,
  input  C_in,
  input  B_Invert,
  input  Less,
  input  [1:0] ALU_Op,
  output ALU_Output,
  output Set,
  output C_out
);

  wire and_1_out, multiplexer_1_out, not_1_out, or_1_out;

  not not_1 (not_1_out, in_1);
  Multiplexer #(.enable("false")) multiplexer_1 (.in0(in_1), .in1(not_1_out), .out(multiplexer_1_out), .sel(B_Invert));
  and and_1 (and_1_out, in_2, in_1);
  or or_1 (or_1_out, in_2, in_1);
  Adder #(.width(1)) adder_1 (.a(in_2), .b(multiplexer_1_out), .out(Set), .cin(C_in), .cout(C_out));
  Multiplexer #(.select(2), .enable("false")) multiplexer_2 (
    .in0(and_1_out), .in1(or_1_out), .in2(Set), .in3(Less), .out(ALU_Output), .sel(ALU_Op));
endmodule

module _16_Bit_ALU (
  input  B_Invert,
  input  [15:0] A,
  input  [15:0] B,
  input  [1:0] ALU_Op,
  output Zero_Flag,
  output [15:0] ALU_Output,
  output Overflow_Flag,
  output C_Out
);

  wire n1_bit_alu_1_c_out, n1_bit_alu_2_c_out, n1_bit_alu_3_c_out, n1_bit_alu_4_c_out, n1_bit_alu_5_c_out,
       n1_bit_alu_6_c_out, n1_bit_alu_7_c_out, n1_bit_alu_8_c_out, n1_bit_alu_9_c_out, n1_bit_alu_10_c_out,
       n1_bit_alu_11_c_out, n1_bit_alu_12_c_out, n1_bit_alu_13_c_out, n1_bit_alu_14_c_out,
       n1_bit_alu_15_c_out, n1_bit_alu_16_set;

  _1_Bit_ALU u_1_bit_alu_1 (
    .C_in(B_Invert), .Less(n1_bit_alu_16_set), .ALU_Output(ALU_Output[0]), .C_out(n1_bit_alu_1_c_out),
    .in_1(B[0]), .in_2(A[0]), .B_Invert(B_Invert), .ALU_Op(ALU_Op));  // open: Set
  _1_Bit_ALU u_1_bit_alu_2 (
    .C_in(n1_bit_alu_1_c_out), .Less(1'b0), .ALU_Output(ALU_Output[1]), .C_out(n1_bit_alu_2_c_out),
    .in_1(B[1]), .in_2(A[1]), .B_Invert(B_Invert), .ALU_Op(ALU_Op));  // open: Set
  _1_Bit_ALU u_1_bit_alu_3 (
    .C_in(n1_bit_alu_2_c_out), .Less(1'b0), .ALU_Output(ALU_Output[2]), .C_out(n1_bit_alu_3_c_out),
    .in_1(B[2]), .in_2(A[2]), .B_Invert(B_Invert), .ALU_Op(ALU_Op));  // open: Set
  _1_Bit_ALU u_1_bit_alu_4 (
    .C_in(n1_bit_alu_3_c_out), .Less(1'b0), .ALU_Output(ALU_Output[3]), .C_out(n1_bit_alu_4_c_out),
    .in_1(B[3]), .in_2(A[3]), .B_Invert(B_Invert), .ALU_Op(ALU_Op));  // open: Set
  _1_Bit_ALU u_1_bit_alu_5 (
    .C_in(n1_bit_alu_4_c_out), .Less(1'b0), .ALU_Output(ALU_Output[4]), .C_out(n1_bit_alu_5_c_out),
    .in_1(B[4]), .in_2(A[4]), .B_Invert(B_Invert), .ALU_Op(ALU_Op));  // open: Set
  _1_Bit_ALU u_1_bit_alu_6 (
    .C_in(n1_bit_alu_5_c_out), .Less(1'b0), .ALU_Output(ALU_Output[5]), .C_out(n1_bit_alu_6_c_out),
    .in_1(B[5]), .in_2(A[5]), .B_Invert(B_Invert), .ALU_Op(ALU_Op));  // open: Set
  _1_Bit_ALU u_1_bit_alu_7 (
    .C_in(n1_bit_alu_6_c_out), .Less(1'b0), .ALU_Output(ALU_Output[6]), .C_out(n1_bit_alu_7_c_out),
    .in_1(B[6]), .in_2(A[6]), .B_Invert(B_Invert), .ALU_Op(ALU_Op));  // open: Set
  _1_Bit_ALU u_1_bit_alu_8 (
    .C_in(n1_bit_alu_7_c_out), .Less(1'b0), .ALU_Output(ALU_Output[7]), .C_out(n1_bit_alu_8_c_out),
    .in_1(B[7]), .in_2(A[7]), .B_Invert(B_Invert), .ALU_Op(ALU_Op));  // open: Set
  _1_Bit_ALU u_1_bit_alu_9 (
    .C_in(n1_bit_alu_8_c_out), .Less(1'b0), .ALU_Output(ALU_Output[8]), .C_out(n1_bit_alu_9_c_out),
    .in_1(B[8]), .in_2(A[8]), .B_Invert(B_Invert), .ALU_Op(ALU_Op));  // open: Set
  _1_Bit_ALU u_1_bit_alu_10 (
    .C_in(n1_bit_alu_9_c_out), .Less(1'b0), .ALU_Output(ALU_Output[9]), .C_out(n1_bit_alu_10_c_out),
    .in_1(B[9]), .in_2(A[9]), .B_Invert(B_Invert), .ALU_Op(ALU_Op));  // open: Set
  _1_Bit_ALU u_1_bit_alu_11 (
    .C_in(n1_bit_alu_10_c_out), .Less(1'b0), .ALU_Output(ALU_Output[10]), .C_out(n1_bit_alu_11_c_out),
    .in_1(B[10]), .in_2(A[10]), .B_Invert(B_Invert), .ALU_Op(ALU_Op));  // open: Set
  _1_Bit_ALU u_1_bit_alu_12 (
    .C_in(n1_bit_alu_11_c_out), .Less(1'b0), .ALU_Output(ALU_Output[11]), .C_out(n1_bit_alu_12_c_out),
    .in_1(B[11]), .in_2(A[11]), .B_Invert(B_Invert), .ALU_Op(ALU_Op));  // open: Set
  _1_Bit_ALU u_1_bit_alu_13 (
    .C_in(n1_bit_alu_12_c_out), .Less(1'b0), .ALU_Output(ALU_Output[12]), .C_out(n1_bit_alu_13_c_out),
    .in_1(B[12]), .in_2(A[12]), .B_Invert(B_Invert), .ALU_Op(ALU_Op));  // open: Set
  _1_Bit_ALU u_1_bit_alu_14 (
    .C_in(n1_bit_alu_13_c_out), .Less(1'b0), .ALU_Output(ALU_Output[13]), .C_out(n1_bit_alu_14_c_out),
    .in_1(B[13]), .in_2(A[13]), .B_Invert(B_Invert), .ALU_Op(ALU_Op));  // open: Set
  _1_Bit_ALU u_1_bit_alu_15 (
    .C_in(n1_bit_alu_14_c_out), .Less(1'b0), .ALU_Output(ALU_Output[14]), .C_out(n1_bit_alu_15_c_out),
    .in_1(B[14]), .in_2(A[14]), .B_Invert(B_Invert), .ALU_Op(ALU_Op));  // open: Set
  _1_Bit_ALU u_1_bit_alu_16 (
    .C_in(n1_bit_alu_15_c_out), .Less(1'b0), .ALU_Output(ALU_Output[15]), .C_out(C_Out), .in_1(B[15]),
    .in_2(A[15]), .B_Invert(B_Invert), .ALU_Op(ALU_Op), .Set(n1_bit_alu_16_set));
  xor xor_1 (Overflow_Flag, n1_bit_alu_15_c_out, C_Out);
  nor nor_1 (Zero_Flag, ALU_Output[0], ALU_Output[1], ALU_Output[2], ALU_Output[3], ALU_Output[4], ALU_Output[5], ALU_Output[6], ALU_Output[7], ALU_Output[8], ALU_Output[9], ALU_Output[10], ALU_Output[11], ALU_Output[12], ALU_Output[13], ALU_Output[14], ALU_Output[15]);

  // Notes on the sheet:
  //   C_In
  //   Set
endmodule
