// Logisim project 16 Bit Register File.circ as structural Verilog
module _16_Bit_Register_File (
  input  RegWrite,
  input  CLK,
  input  [15:0] Write_Data,
  input  [3:0] Read_Register_1,
  input  [3:0] Write_Register,
  input  [3:0] Read_Register_2,
  output [15:0] Read_Data_1,
  output [15:0] Read_Data_2
);

  wire and_1_out, and_2_out, and_3_out, and_4_out, and_5_out, and_6_out, and_7_out, and_8_out, and_9_out,
       and_10_out, and_11_out, and_12_out, and_13_out, and_14_out, and_15_out, and_16_out, decoder_1_out0,
       decoder_1_out1, decoder_1_out2, decoder_1_out3, decoder_1_out4, decoder_1_out5, decoder_1_out6,
       decoder_1_out7, decoder_1_out8, decoder_1_out9, decoder_1_out10, decoder_1_out11, decoder_1_out12,
       decoder_1_out13, decoder_1_out14, decoder_1_out15;
  wire [15:0] _0_q, _1_q, _2_q, _3_q, _4_q, _5_q, _6_q, _7_q, _8_q, _9_q, _10_q, _11_q, _12_q, _13_q, _14_q,
       _15_q;

  Decoder #(.select(4), .enable("false")) decoder_1 (
    .out0(decoder_1_out0), .out1(decoder_1_out1), .out2(decoder_1_out2), .out3(decoder_1_out3),
    .out4(decoder_1_out4), .out5(decoder_1_out5), .out6(decoder_1_out6), .out7(decoder_1_out7),
    .out8(decoder_1_out8), .out9(decoder_1_out9), .out10(decoder_1_out10), .out11(decoder_1_out11),
    .out12(decoder_1_out12), .out13(decoder_1_out13), .out14(decoder_1_out14), .out15(decoder_1_out15),
    .sel(Write_Register));
  and and_1 (and_1_out, decoder_1_out0, RegWrite);
  and and_2 (and_2_out, decoder_1_out1, RegWrite);
  and and_3 (and_3_out, decoder_1_out2, RegWrite);
  and and_4 (and_4_out, decoder_1_out3, RegWrite);
  and and_5 (and_5_out, decoder_1_out4, RegWrite);
  and and_6 (and_6_out, decoder_1_out5, RegWrite);
  and and_7 (and_7_out, decoder_1_out6, RegWrite);
  and and_8 (and_8_out, decoder_1_out7, RegWrite);
  and and_9 (and_9_out, decoder_1_out8, RegWrite);
  and and_10 (and_10_out, decoder_1_out9, RegWrite);
  and and_11 (and_11_out, decoder_1_out10, RegWrite);
  and and_12 (and_12_out, decoder_1_out11, RegWrite);
  and and_13 (and_13_out, decoder_1_out12, RegWrite);
  and and_14 (and_14_out, decoder_1_out13, RegWrite);
  and and_15 (and_15_out, decoder_1_out14, RegWrite);
  and and_16 (and_16_out, decoder_1_out15, RegWrite);
  Register #(.width(16)) _0 (.D(Write_Data), .en(and_1_out), .Q(_0_q), .clk(CLK));  // open: clr
  Register #(.width(16)) _1 (.D(Write_Data), .en(and_2_out), .Q(_1_q), .clk(CLK));  // open: clr
  Register #(.width(16)) _2 (.D(Write_Data), .en(and_3_out), .Q(_2_q), .clk(CLK));  // open: clr
  Register #(.width(16)) _3 (.D(Write_Data), .en(and_4_out), .Q(_3_q), .clk(CLK));  // open: clr
  Register #(.width(16)) _4 (.D(Write_Data), .en(and_5_out), .Q(_4_q), .clk(CLK));  // open: clr
  Register #(.width(16)) _5 (.D(Write_Data), .en(and_6_out), .Q(_5_q), .clk(CLK));  // open: clr
  Register #(.width(16)) _6 (.D(Write_Data), .en(and_7_out), .Q(_6_q), .clk(CLK));  // open: clr
  Register #(.width(16)) _7 (.D(Write_Data), .en(and_8_out), .Q(_7_q), .clk(CLK));  // open: clr
  Register #(.width(16)) _8 (.D(Write_Data), .en(and_9_out), .Q(_8_q), .clk(CLK));  // open: clr
  Register #(.width(16)) _9 (.D(Write_Data), .en(and_10_out), .Q(_9_q), .clk(CLK));  // open: clr
  Register #(.width(16)) _10 (.D(Write_Data), .en(and_11_out), .Q(_10_q), .clk(CLK));  // open: clr
  Register #(.width(16)) _11 (.D(Write_Data), .en(and_12_out), .Q(_11_q), .clk(CLK));  // open: clr
  Register #(.width(16)) _12 (.D(Write_Data), .en(and_13_out), .Q(_12_q), .clk(CLK));  // open: clr
  Register #(.width(16)) _13 (.D(Write_Data), .en(and_14_out), .Q(_13_q), .clk(CLK));  // open: clr
  Register #(.width(16)) _14 (.D(Write_Data), .en(and_15_out), .Q(_14_q), .clk(CLK));  // open: clr
  Register #(.width(16)) _15 (.D(Write_Data), .en(and_16_out), .Q(_15_q), .clk(CLK));  // open: clr
  Multiplexer #(.select(4), .width(16), .enable("false")) multiplexer_1 (
    .in0(_0_q), .in1(_1_q), .in2(_2_q), .in3(_3_q), .in4(_4_q), .in5(_5_q), .in6(_6_q), .in7(_7_q),
    .in8(_8_q), .in9(_9_q), .in10(_10_q), .in11(_11_q), .in12(_12_q), .in13(_13_q), .in14(_14_q),
    .in15(_15_q), .out(Read_Data_1), .sel(Read_Register_1));
  Multiplexer #(.select(4), .width(16), .enable("false")) multiplexer_2 (
    .in0(_0_q), .in1(_1_q), .in2(_2_q), .in3(_3_q), .in4(_4_q), .in5(_5_q), .in6(_6_q), .in7(_7_q),
    .in8(_8_q), .in9(_9_q), .in10(_10_q), .in11(_11_q), .in12(_12_q), .in13(_13_q), .in14(_14_q),
    .in15(_15_q), .out(Read_Data_2), .sel(Read_Register_2));
endmodule
