// Logisim project Control Unit.circ as structural Verilog
module main (
  input  in_1,
  input  in_2,
  input  in_3,
  output out_4,
  output out_5,
  output out_6,
  output out_7,
  output out_8,
  output out_9,
  output out_10,
  output out_11,
  output out_12
);

  wire not_1_out, not_2_out, not_3_out, not_4_out, not_5_out, not_6_out, not_7_out, not_8_out, not_9_out,
       not_10_out;

  not not_1 (not_1_out, in_2);
  not not_2 (not_2_out, in_1);
  and and_1 (out_4, not_2_out, not_1_out, not_3_out);
  not not_3 (not_3_out, in_3);
  not not_4 (not_4_out, in_1);
  not not_5 (not_5_out, in_1);
  not not_6 (not_6_out, in_1);
  and and_2 (out_7, not_4_out, not_5_out, in_1);
  not not_7 (not_7_out, in_1);
  and and_3 (out_8, not_6_out, in_2, not_7_out);
  not not_8 (not_8_out, in_1);
  and and_4 (out_9, not_8_out, in_2, in_2);
  not not_9 (not_9_out, in_2);
  not not_10 (not_10_out, in_2);
  and and_5 (out_10, in_1, not_10_out, not_9_out);
  or or_1 (out_5, out_4, out_7);
  or or_2 (out_6, out_7, out_8);

  assign out_11 = out_4;
  assign out_12 = out_9;

  // Notes on the sheet:
  //   R-Type
  //   LW
  //   SW
  //   Beq
  //   Jump
  //   RegDst
  //   RegWrite
  //   ALU SRC
  //   Memread
  //   MemWrite
  //   BEQ
  //   JUMP
  //   ALU-OP-1
  //   ALU-OP-2
endmodule
