// Logisim project Datapath[R-Type].circ as structural Verilog: 1 circuit, main circuit main
module main (
  input  in_1,
  input  RegWrite,
  output [15:0] Read_Data_1,
  output [3:0] RS,
  output Zero_Flag,
  output [15:0] ALU_Output,
  output Overflow_Flag,
  output C_Out,
  output [15:0] Read_Data_2,
  output [3:0] RT,
  output [3:0] RD,
  output [2:0] out_12
);

  wire CLK_out;
  wire [15:0] adder_1_out, PC_q;
  wire [15:15] rom_1_data;

  Register #(.width(16)) PC (.D(adder_1_out), .Q(PC_q), .clk(CLK_out));  // open: en, clr
  Adder #(.width(16)) adder_1 (.a(PC_q), .b(16'h1), .out(adder_1_out), .cin(in_1));  // open: cout
  ROM #(.addrWidth(16), .dataWidth(16)) rom_1 (.addr(PC_q), .data({rom_1_data[15], out_12, RS, RT, RD}));  // open: sel
  Clock CLK (.out(CLK_out));
  _16_Bit_Register_File u_16_bit_register_file_1 (
    .Write_Data(ALU_Output), .Read_Data_1(Read_Data_1), .Read_Register_1(RS), .Read_Data_2(Read_Data_2),
    .Read_Register_2(RT), .RegWrite(RegWrite), .CLK(CLK_out), .Write_Register(RD));
  _16_Bit_ALU u_16_bit_alu_1 (
    .A(Read_Data_1), .B(Read_Data_2), .Zero_Flag(Zero_Flag), .ALU_Output(ALU_Output),
    .Overflow_Flag(Overflow_Flag), .C_Out(C_Out), .B_Invert(out_12[2]), .ALU_Op(out_12[1:0]));

  // Notes on the sheet:
  //   ISA
  //   Opcode
  //   0001==>OR
  //   0000 ==> AND
  //   0010==>ADD
  //   0110==>SUB
  //   contents of rom_1 (hex, n*v repeats v):
  //   123 321 564 234 3333
  //   OpCode
endmodule
