// Logisim project Project2.circ as structural Verilog: 10 circuits, main circuit main
module main (
  input  [15:0] Rs_Value,
  input  [15:0] Rt_Value,
  input  [3:0] Rs,
  input  [3:0] Rt,
  input  [3:0] Rd,
  input  [3:0] OPCODE,
  input  in_7
);

  wire clock_1_out, decoder_1_out0, decoder_1_out1, decoder_1_out2, decoder_1_out3, decoder_1_out4,
       decoder_1_out5, decoder_1_out6, decoder_1_out7, decoder_1_out8, decoder_1_out9, decoder_1_out10,
       decoder_1_out11;
  wire [1:0] counter_1_q;
  wire [3:0] multiplexer_1_out;
  wire [15:0] adder_1_out_3, adder_2_out_3, and_1_out, and_2_out, bit_extender_1_out, multiplexer_2_out,
       multiplexer_3_out, multiplexer_4_out, multiplexer_5_out, nor_1_out, or_1_out, or_2_out, s0_q, s1_q,
       s2_q, s3_q, s4_q, s5_q, subtractor_1_out_3, t0_q, t1_q, t2_q, t3_q, t4_q, zero_q;

  Counter #(.width(2), .max('h3)) counter_1 (.Q(counter_1_q), .clk(clock_1_out));  // open: load, D, count, carry, clr
  Clock clock_1 (.out(clock_1_out));
  Multiplexer #(.select(2), .width(4), .enable("false")) multiplexer_1 (
    .in0(Rs), .in1(Rt), .in2(Rd), .out(multiplexer_1_out), .sel(counter_1_q));  // open: in3
  Decoder #(.select(4), .enable("false")) decoder_1 (
    .out0(decoder_1_out0), .out1(decoder_1_out1), .out2(decoder_1_out2), .out3(decoder_1_out3),
    .out4(decoder_1_out4), .out5(decoder_1_out5), .out6(decoder_1_out6), .out7(decoder_1_out7),
    .out8(decoder_1_out8), .out9(decoder_1_out9), .out10(decoder_1_out10), .out11(decoder_1_out11),
    .sel(multiplexer_1_out));  // open: out12, out13, out14, out15
  Multiplexer #(.select(2), .width(16), .enable("false")) multiplexer_2 (
    .in0(Rs_Value), .in1(Rt_Value), .in2(multiplexer_5_out), .out(multiplexer_2_out), .sel(counter_1_q));  // open: in3
  Register #(.width(16)) zero (.en(decoder_1_out0), .Q(zero_q), .clk(clock_1_out), .clr(in_7));  // open: D
  Register #(.width(16)) s0 (.D(multiplexer_2_out), .en(decoder_1_out1), .Q(s0_q), .clk(clock_1_out), .clr(in_7));
  Register #(.width(16)) s1 (.D(multiplexer_2_out), .en(decoder_1_out2), .Q(s1_q), .clk(clock_1_out), .clr(in_7));
  Register #(.width(16)) s2 (.D(multiplexer_2_out), .en(decoder_1_out3), .Q(s2_q), .clk(clock_1_out), .clr(in_7));
  Register #(.width(16)) s3 (.D(multiplexer_2_out), .en(decoder_1_out4), .Q(s3_q), .clk(clock_1_out), .clr(in_7));
  Register #(.width(16)) s4 (.D(multiplexer_2_out), .en(decoder_1_out5), .Q(s4_q), .clk(clock_1_out), .clr(in_7));
  Register #(.width(16)) s5 (.D(multiplexer_2_out), .en(decoder_1_out6), .Q(s5_q), .clk(clock_1_out), .clr(in_7));
  Register #(.width(16)) t0 (.D(multiplexer_2_out), .en(decoder_1_out7), .Q(t0_q), .clk(clock_1_out), .clr(in_7));
  Register #(.width(16)) t1 (.D(multiplexer_2_out), .en(decoder_1_out8), .Q(t1_q), .clk(clock_1_out), .clr(in_7));
  Register #(.width(16)) t2 (.D(multiplexer_2_out), .en(decoder_1_out9), .Q(t2_q), .clk(clock_1_out), .clr(in_7));
  Register #(.width(16)) t3 (.D(multiplexer_2_out), .en(decoder_1_out10), .Q(t3_q), .clk(clock_1_out), .clr(in_7));
  Register #(.width(16)) t4 (.D(multiplexer_2_out), .en(decoder_1_out11), .Q(t4_q), .clk(clock_1_out), .clr(in_7));
  assign bit_extender_1_out = {{12{1'b0}}, Rt};  // Bit_Extender bit_extender_1
  Multiplexer #(.select(4), .width(16), .enable("false")) multiplexer_3 (
    .in0(zero_q), .in1(s0_q), .in2(s1_q), .in3(s2_q), .in4(s3_q), .in5(s4_q), .in6(s5_q), .in7(t0_q),
    .in8(t1_q), .in9(t2_q), .in10(t3_q), .in11(t4_q), .out(multiplexer_3_out), .sel(Rs));  // open: in12, in13, in14, in15
  Multiplexer #(.select(4), .width(16), .enable("false")) multiplexer_4 (
    .in0(zero_q), .in1(s0_q), .in2(s1_q), .in3(s2_q), .in4(s3_q), .in5(s4_q), .in6(s5_q), .in7(t0_q),
    .in8(t1_q), .in9(t2_q), .in10(t3_q), .in11(t4_q), .out(multiplexer_4_out), .sel(Rt));  // open: in12, in13, in14, in15
  Adder adder_1 (.A(multiplexer_4_out), .B(multiplexer_3_out), .out_3(adder_1_out_3));
  Subtractor subtractor_1 (.in_1(multiplexer_3_out), .in_2(multiplexer_4_out), .out_3(subtractor_1_out_3));
  assign and_1_out = multiplexer_3_out & multiplexer_4_out;  // AND_Gate and_1, 16 bits wide
  assign or_1_out = multiplexer_3_out | multiplexer_4_out;  // OR_Gate or_1, 16 bits wide
  assign and_2_out = multiplexer_3_out & bit_extender_1_out;  // AND_Gate and_2, 16 bits wide
  assign or_2_out = multiplexer_3_out | bit_extender_1_out;  // OR_Gate or_2, 16 bits wide
  Adder adder_2 (.A(multiplexer_3_out), .B(bit_extender_1_out), .out_3(adder_2_out_3));
  assign nor_1_out = ~(multiplexer_3_out | multiplexer_4_out);  // NOR_Gate nor_1, 16 bits wide
  Multiplexer #(.select(4), .width(16), .enable("false")) multiplexer_5 (
    .in0(adder_1_out_3), .in1(subtractor_1_out_3), .in2(and_1_out), .in3(or_1_out), .in4(nor_1_out),
    .in8(and_2_out), .in9(or_2_out), .in10(adder_2_out_3), .out(multiplexer_5_out), .sel(OPCODE));  // open: in5, in6, in7, in11, in12, in13, in14, in15
endmodule

module Adder (
  input  [15:0] A,
  input  [15:0] B,
  output [15:0] out_3
);

  wire carry_look_ahead_1_c1, carry_look_ahead_1_c2, carry_look_ahead_1_c3, carry_look_ahead_1_out_4,
       carry_look_ahead_2_c1, carry_look_ahead_2_c2, carry_look_ahead_2_c3, carry_look_ahead_2_out_4,
       carry_look_ahead_3_c1, carry_look_ahead_3_c2, carry_look_ahead_3_c3, carry_look_ahead_3_out_4,
       carry_look_ahead_4_c1, carry_look_ahead_4_c2, carry_look_ahead_4_out_4, xor_1_out, xor_2_out,
       xor_3_out, xor_4_out, xor_5_out, xor_6_out, xor_7_out, xor_8_out, xor_9_out, xor_10_out, xor_11_out,
       xor_12_out, xor_13_out, xor_14_out, xor_15_out, xor_16_out;

  Carry_Look_Ahead carry_look_ahead_1 (
    .Cin(1'b0), .in_2(A[3:0]), .in_3(B[3:0]), .out_4(carry_look_ahead_1_out_4), .C1(carry_look_ahead_1_c1),
    .C2(carry_look_ahead_1_c2), .C3(carry_look_ahead_1_c3));
  Carry_Look_Ahead carry_look_ahead_2 (
    .Cin(carry_look_ahead_1_c3), .in_2(A[7:4]), .in_3(B[7:4]), .out_4(carry_look_ahead_2_out_4),
    .C1(carry_look_ahead_2_c1), .C2(carry_look_ahead_2_c2), .C3(carry_look_ahead_2_c3));
  Carry_Look_Ahead carry_look_ahead_3 (
    .Cin(carry_look_ahead_2_c3), .in_2(A[11:8]), .in_3(B[11:8]), .out_4(carry_look_ahead_3_out_4),
    .C1(carry_look_ahead_3_c1), .C2(carry_look_ahead_3_c2), .C3(carry_look_ahead_3_c3));
  Carry_Look_Ahead carry_look_ahead_4 (
    .Cin(carry_look_ahead_3_c3), .in_2(A[15:12]), .in_3(B[15:12]), .out_4(carry_look_ahead_4_out_4),
    .C1(carry_look_ahead_4_c1), .C2(carry_look_ahead_4_c2));  // open: C3
  xor xor_1 (xor_1_out, A[0], 1'b0);
  xor xor_2 (xor_2_out, A[1], carry_look_ahead_1_out_4);
  xor xor_3 (xor_3_out, A[2], carry_look_ahead_1_c1);
  xor xor_4 (xor_4_out, A[3], carry_look_ahead_1_c2);
  xor xor_5 (xor_5_out, A[4], carry_look_ahead_1_c3);
  xor xor_6 (xor_6_out, A[5], carry_look_ahead_2_out_4);
  xor xor_7 (xor_7_out, A[6], carry_look_ahead_2_c1);
  xor xor_8 (xor_8_out, A[7], carry_look_ahead_2_c2);
  xor xor_9 (xor_9_out, A[8], carry_look_ahead_2_c3);
  xor xor_10 (xor_10_out, A[9], carry_look_ahead_3_out_4);
  xor xor_11 (xor_11_out, A[10], carry_look_ahead_3_c1);
  xor xor_12 (xor_12_out, A[11], carry_look_ahead_3_c2);
  xor xor_13 (xor_13_out, A[12], carry_look_ahead_3_c3);
  xor xor_14 (xor_14_out, A[13], carry_look_ahead_4_out_4);
  xor xor_15 (xor_15_out, A[14], carry_look_ahead_4_c1);
  xor xor_16 (xor_16_out, A[15], carry_look_ahead_4_c2);
  xor xor_17 (out_3[0], xor_1_out, B[0]);
  xor xor_18 (out_3[1], xor_2_out, B[1]);
  xor xor_19 (out_3[2], xor_3_out, B[2]);
  xor xor_20 (out_3[3], xor_4_out, B[3]);
  xor xor_21 (out_3[4], xor_5_out, B[4]);
  xor xor_22 (out_3[5], xor_6_out, B[5]);
  xor xor_23 (out_3[6], xor_7_out, B[6]);
  xor xor_24 (out_3[7], xor_8_out, B[7]);
  xor xor_25 (out_3[8], xor_9_out, B[8]);
  xor xor_26 (out_3[9], xor_10_out, B[9]);
  xor xor_27 (out_3[10], xor_11_out, B[10]);
  xor xor_28 (out_3[11], xor_12_out, B[11]);
  xor xor_29 (out_3[12], xor_13_out, B[12]);
  xor xor_30 (out_3[13], xor_14_out, B[13]);
  xor xor_31 (out_3[14], xor_15_out, B[14]);
  xor xor_32 (out_3[15], xor_16_out, B[15]);
endmodule

module Subtractor (
  input  [15:0] in_1,
  input  [15:0] in_2,
  output [15:0] out_3
);

  wire [15:0] not_1_out;

  assign not_1_out = ~in_2;  // NOT_Gate not_1, 16 bits wide
  Adder adder_1 (.A(in_1), .B(not_1_out), .out_3(out_3));
endmodule

module Sll (
  input  [15:0] in_1,
  input  [3:0] in_2,
  output [15:0] out_3
);

  Multiplexer #(.select(4), .enable("false")) multiplexer_1 (
    .in0(in_1[0]), .in1(1'b0), .in2(1'b0), .in3(1'b0), .in4(1'b0), .in5(1'b0), .in6(1'b0), .in7(1'b0),
    .in8(1'b0), .in9(1'b0), .in10(1'b0), .in11(1'b0), .in12(1'b0), .in13(1'b0), .in14(1'b0), .in15(1'b0),
    .out(out_3[0]), .sel(in_2));
  Multiplexer #(.select(4), .enable("false")) multiplexer_2 (
    .in0(in_1[1]), .in1(in_1[0]), .in2(1'b0), .in3(1'b0), .in4(1'b0), .in5(1'b0), .in6(1'b0), .in7(1'b0),
    .in8(1'b0), .in9(1'b0), .in10(1'b0), .in11(1'b0), .in12(1'b0), .in13(1'b0), .in14(1'b0), .in15(1'b0),
    .out(out_3[1]), .sel(in_2));
  Multiplexer #(.select(4), .enable("false")) multiplexer_3 (
    .in0(in_1[2]), .in1(in_1[1]), .in2(in_1[0]), .in3(1'b0), .in4(1'b0), .in5(1'b0), .in6(1'b0), .in7(1'b0),
    .in8(1'b0), .in9(1'b0), .in10(1'b0), .in11(1'b0), .in12(1'b0), .in13(1'b0), .in14(1'b0), .in15(1'b0),
    .out(out_3[2]), .sel(in_2));
  Multiplexer #(.select(4), .enable("false")) multiplexer_4 (
    .in0(in_1[3]), .in1(in_1[2]), .in2(in_1[1]), .in3(in_1[0]), .in4(1'b0), .in5(1'b0), .in6(1'b0),
    .in7(1'b0), .in8(1'b0), .in9(1'b0), .in10(1'b0), .in11(1'b0), .in12(1'b0), .in13(1'b0), .in14(1'b0),
    .in15(1'b0), .out(out_3[3]), .sel(in_2));
  Multiplexer #(.select(4), .enable("false")) multiplexer_5 (
    .in0(in_1[4]), .in1(in_1[3]), .in2(in_1[2]), .in3(in_1[1]), .in4(in_1[0]), .in5(1'b0), .in6(1'b0),
    .in7(1'b0), .in8(1'b0), .in9(1'b0), .in10(1'b0), .in11(1'b0), .in12(1'b0), .in13(1'b0), .in14(1'b0),
    .in15(1'b0), .out(out_3[4]), .sel(in_2));
  Multiplexer #(.select(4), .enable("false")) multiplexer_6 (
    .in0(in_1[5]), .in1(in_1[4]), .in2(in_1[3]), .in3(in_1[2]), .in4(in_1[1]), .in5(in_1[0]), .in6(1'b0),
    .in7(1'b0), .in8(1'b0), .in9(1'b0), .in10(1'b0), .in11(1'b0), .in12(1'b0), .in13(1'b0), .in14(1'b0),
    .in15(1'b0), .out(out_3[5]), .sel(in_2));
  Multiplexer #(.select(4), .enable("false")) multiplexer_7 (
    .in0(in_1[6]), .in1(in_1[5]), .in2(in_1[4]), .in3(in_1[3]), .in4(in_1[2]), .in5(in_1[1]), .in6(in_1[0]),
    .in7(1'b0), .in8(1'b0), .in9(1'b0), .in10(1'b0), .in11(1'b0), .in12(1'b0), .in13(1'b0), .in14(1'b0),
    .in15(1'b0), .out(out_3[6]), .sel(in_2));
  Multiplexer #(.select(4), .enable("false")) multiplexer_8 (
    .in0(in_1[7]), .in1(in_1[6]), .in2(in_1[5]), .in3(in_1[4]), .in4(in_1[3]), .in5(in_1[2]), .in6(in_1[1]),
    .in7(in_1[0]), .in8(1'b0), .in9(1'b0), .in10(1'b0), .in11(1'b0), .in12(1'b0), .in13(1'b0), .in14(1'b0),
    .in15(1'b0), .out(out_3[7]), .sel(in_2));
  Multiplexer #(.select(4), .enable("false")) multiplexer_9 (
    .in0(in_1[8]), .in1(in_1[7]), .in2(in_1[6]), .in3(in_1[5]), .in4(in_1[4]), .in5(in_1[3]), .in6(in_1[2]),
    .in7(in_1[1]), .in8(in_1[0]), .in9(1'b0), .in10(1'b0), .in11(1'b0), .in12(1'b0), .in13(1'b0),
    .in14(1'b0), .in15(1'b0), .out(out_3[8]), .sel(in_2));
  Multiplexer #(.select(4), .enable("false")) multiplexer_10 (
    .in0(in_1[9]), .in1(in_1[8]), .in2(in_1[7]), .in3(in_1[6]), .in4(in_1[5]), .in5(in_1[4]), .in6(in_1[3]),
    .in7(in_1[2]), .in8(in_1[1]), .in9(in_1[0]), .in10(1'b0), .in11(1'b0), .in12(1'b0), .in13(1'b0),
    .in14(1'b0), .in15(1'b0), .out(out_3[9]), .sel(in_2));
  Multiplexer #(.select(4), .enable("false")) multiplexer_11 (
    .in0(in_1[10]), .in1(in_1[9]), .in2(in_1[8]), .in3(in_1[7]), .in4(in_1[6]), .in5(in_1[5]), .in6(in_1[4]),
    .in7(in_1[3]), .in8(in_1[2]), .in9(in_1[1]), .in10(in_1[0]), .in11(1'b0), .in12(1'b0), .in13(1'b0),
    .in14(1'b0), .in15(1'b0), .out(out_3[10]), .sel(in_2));
  Multiplexer #(.select(4), .enable("false")) multiplexer_12 (
    .in0(in_1[11]), .in1(in_1[10]), .in2(in_1[9]), .in3(in_1[8]), .in4(in_1[7]), .in5(in_1[6]),
    .in6(in_1[5]), .in7(in_1[4]), .in8(in_1[3]), .in9(in_1[2]), .in10(in_1[1]), .in11(in_1[0]), .in12(1'b0),
    .in13(1'b0), .in14(1'b0), .in15(1'b0), .out(out_3[11]), .sel(in_2));
  Multiplexer #(.select(4), .enable("false")) multiplexer_13 (
    .in0(in_1[12]), .in1(in_1[11]), .in2(in_1[10]), .in3(in_1[9]), .in4(in_1[8]), .in5(in_1[7]),
    .in6(in_1[6]), .in7(in_1[5]), .in8(in_1[4]), .in9(in_1[3]), .in10(in_1[2]), .in11(in_1[1]),
    .in12(in_1[0]), .in13(1'b0), .in14(1'b0), .in15(1'b0), .out(out_3[12]), .sel(in_2));
  Multiplexer #(.select(4), .enable("false")) multiplexer_14 (
    .in0(in_1[13]), .in1(in_1[12]), .in2(in_1[11]), .in3(in_1[10]), .in4(in_1[9]), .in5(in_1[8]),
    .in6(in_1[7]), .in7(in_1[6]), .in8(in_1[5]), .in9(in_1[4]), .in10(in_1[3]), .in11(in_1[2]),
    .in12(in_1[1]), .in13(in_1[0]), .in14(1'b0), .in15(1'b0), .out(out_3[13]), .sel(in_2));
  Multiplexer #(.select(4), .enable("false")) multiplexer_15 (
    .in0(in_1[14]), .in1(in_1[13]), .in2(in_1[12]), .in3(in_1[11]), .in4(in_1[10]), .in5(in_1[9]),
    .in6(in_1[8]), .in7(in_1[7]), .in8(in_1[6]), .in9(in_1[5]), .in10(in_1[4]), .in11(in_1[3]),
    .in12(in_1[2]), .in13(in_1[1]), .in14(in_1[0]), .in15(1'b0), .out(out_3[14]), .sel(in_2));
  Multiplexer #(.select(4), .enable("false")) multiplexer_16 (
    .in0(in_1[15]), .in1(in_1[14]), .in2(in_1[13]), .in3(in_1[12]), .in4(in_1[11]), .in5(in_1[10]),
    .in6(in_1[9]), .in7(in_1[8]), .in8(in_1[7]), .in9(in_1[6]), .in10(in_1[5]), .in11(in_1[4]),
    .in12(in_1[3]), .in13(in_1[2]), .in14(in_1[1]), .in15(in_1[0]), .out(out_3[15]), .sel(in_2));
endmodule

module Srl (
  input  [15:0] in_1,
  input  [3:0] in_2,
  output [15:0] out_3
);

  Multiplexer #(.select(4), .enable("false")) multiplexer_1 (
    .in0(in_1[0]), .in1(in_1[1]), .in2(in_1[2]), .in3(in_1[3]), .in4(in_1[4]), .in5(in_1[5]), .in6(in_1[6]),
    .in7(in_1[7]), .in8(in_1[8]), .in9(in_1[9]), .in10(in_1[10]), .in11(in_1[11]), .in12(in_1[12]),
    .in13(in_1[13]), .in14(in_1[14]), .in15(in_1[15]), .out(out_3[0]), .sel(in_2));
  Multiplexer #(.select(4), .enable("false")) multiplexer_2 (
    .in0(in_1[1]), .in1(in_1[2]), .in2(in_1[3]), .in3(in_1[4]), .in4(in_1[5]), .in5(in_1[6]), .in6(in_1[7]),
    .in7(in_1[8]), .in8(in_1[9]), .in9(in_1[10]), .in10(in_1[11]), .in11(in_1[12]), .in12(in_1[13]),
    .in13(in_1[14]), .in14(in_1[15]), .in15(1'b0), .out(out_3[1]), .sel(in_2));
  Multiplexer #(.select(4), .enable("false")) multiplexer_3 (
    .in0(in_1[2]), .in1(in_1[3]), .in2(in_1[4]), .in3(in_1[5]), .in4(in_1[6]), .in5(in_1[7]), .in6(in_1[8]),
    .in7(in_1[9]), .in8(in_1[10]), .in9(in_1[11]), .in10(in_1[12]), .in11(in_1[13]), .in12(in_1[14]),
    .in13(in_1[15]), .in14(1'b0), .in15(1'b0), .out(out_3[2]), .sel(in_2));
  Multiplexer #(.select(4), .enable("false")) multiplexer_4 (
    .in0(in_1[3]), .in1(in_1[4]), .in2(in_1[5]), .in3(in_1[6]), .in4(in_1[7]), .in5(in_1[8]), .in6(in_1[9]),
    .in7(in_1[10]), .in8(in_1[11]), .in9(in_1[12]), .in10(in_1[13]), .in11(in_1[14]), .in12(in_1[15]),
    .in13(1'b0), .in14(1'b0), .in15(1'b0), .out(out_3[3]), .sel(in_2));
  Multiplexer #(.select(4), .enable("false")) multiplexer_5 (
    .in0(in_1[4]), .in1(in_1[5]), .in2(in_1[6]), .in3(in_1[7]), .in4(in_1[8]), .in5(in_1[9]), .in6(in_1[10]),
    .in7(in_1[11]), .in8(in_1[12]), .in9(in_1[13]), .in10(in_1[14]), .in11(in_1[15]), .in12(1'b0),
    .in13(1'b0), .in14(1'b0), .in15(1'b0), .out(out_3[4]), .sel(in_2));
  Multiplexer #(.select(4), .enable("false")) multiplexer_6 (
    .in0(in_1[5]), .in1(in_1[6]), .in2(in_1[7]), .in3(in_1[8]), .in4(in_1[9]), .in5(in_1[10]),
    .in6(in_1[11]), .in7(in_1[12]), .in8(in_1[13]), .in9(in_1[14]), .in10(in_1[15]), .in11(1'b0),
    .in12(1'b0), .in13(1'b0), .in14(1'b0), .in15(1'b0), .out(out_3[5]), .sel(in_2));
  Multiplexer #(.select(4), .enable("false")) multiplexer_7 (
    .in0(in_1[6]), .in1(in_1[7]), .in2(in_1[8]), .in3(in_1[9]), .in4(in_1[10]), .in5(in_1[11]),
    .in6(in_1[12]), .in7(in_1[13]), .in8(in_1[14]), .in9(in_1[15]), .in10(1'b0), .in11(1'b0), .in12(1'b0),
    .in13(1'b0), .in14(1'b0), .in15(1'b0), .out(out_3[6]), .sel(in_2));
  Multiplexer #(.select(4), .enable("false")) multiplexer_8 (
    .in0(in_1[7]), .in1(in_1[8]), .in2(in_1[9]), .in3(in_1[10]), .in4(in_1[11]), .in5(in_1[12]),
    .in6(in_1[13]), .in7(in_1[14]), .in8(in_1[15]), .in9(1'b0), .in10(1'b0), .in11(1'b0), .in12(1'b0),
    .in13(1'b0), .in14(1'b0), .in15(1'b0), .out(out_3[7]), .sel(in_2));
  Multiplexer #(.select(4), .enable("false")) multiplexer_9 (
    .in0(in_1[8]), .in1(in_1[9]), .in2(in_1[10]), .in3(in_1[11]), .in4(in_1[12]), .in5(in_1[13]),
    .in6(in_1[14]), .in7(in_1[15]), .in8(1'b0), .in9(1'b0), .in10(1'b0), .in11(1'b0), .in12(1'b0),
    .in13(1'b0), .in14(1'b0), .in15(1'b0), .out(out_3[8]), .sel(in_2));
  Multiplexer #(.select(4), .enable("false")) multiplexer_10 (
    .in0(in_1[9]), .in1(in_1[10]), .in2(in_1[11]), .in3(in_1[12]), .in4(in_1[13]), .in5(in_1[14]),
    .in6(in_1[15]), .in7(1'b0), .in8(1'b0), .in9(1'b0), .in10(1'b0), .in11(1'b0), .in12(1'b0), .in13(1'b0),
    .in14(1'b0), .in15(1'b0), .out(out_3[9]), .sel(in_2));
  Multiplexer #(.select(4), .enable("false")) multiplexer_11 (
    .in0(in_1[10]), .in1(in_1[11]), .in2(in_1[12]), .in3(in_1[13]), .in4(in_1[14]), .in5(in_1[15]),
    .in6(1'b0), .in7(1'b0), .in8(1'b0), .in9(1'b0), .in10(1'b0), .in11(1'b0), .in12(1'b0), .in13(1'b0),
    .in14(1'b0), .in15(1'b0), .out(out_3[10]), .sel(in_2));
  Multiplexer #(.select(4), .enable("false")) multiplexer_12 (
    .in0(in_1[11]), .in1(in_1[12]), .in2(in_1[13]), .in3(in_1[14]), .in4(in_1[15]), .in5(1'b0), .in6(1'b0),
    .in7(1'b0), .in8(1'b0), .in9(1'b0), .in10(1'b0), .in11(1'b0), .in12(1'b0), .in13(1'b0), .in14(1'b0),
    .in15(1'b0), .out(out_3[11]), .sel(in_2));
  Multiplexer #(.select(4), .enable("false")) multiplexer_13 (
    .in0(in_1[12]), .in1(in_1[13]), .in2(in_1[14]), .in3(in_1[15]), .in4(1'b0), .in5(1'b0), .in6(1'b0),
    .in7(1'b0), .in8(1'b0), .in9(1'b0), .in10(1'b0), .in11(1'b0), .in12(1'b0), .in13(1'b0), .in14(1'b0),
    .in15(1'b0), .out(out_3[12]), .sel(in_2));
  Multiplexer #(.select(4), .enable("false")) multiplexer_14 (
    .in0(in_1[13]), .in1(in_1[14]), .in2(in_1[15]), .in3(1'b0), .in4(1'b0), .in5(1'b0), .in6(1'b0),
    .in7(1'b0), .in8(1'b0), .in9(1'b0), .in10(1'b0), .in11(1'b0), .in12(1'b0), .in13(1'b0), .in14(1'b0),
    .in15(1'b0), .out(out_3[13]), .sel(in_2));
  Multiplexer #(.select(4), .enable("false")) multiplexer_15 (
    .in0(in_1[14]), .in1(in_1[15]), .in2(1'b0), .in3(1'b0), .in4(1'b0), .in5(1'b0), .in6(1'b0), .in7(1'b0),
    .in8(1'b0), .in9(1'b0), .in10(1'b0), .in11(1'b0), .in12(1'b0), .in13(1'b0), .in14(1'b0), .in15(1'b0),
    .out(out_3[14]), .sel(in_2));
  Multiplexer #(.select(4), .enable("false")) multiplexer_16 (
    .in0(in_1[15]), .in1(1'b0), .in2(1'b0), .in3(1'b0), .in4(1'b0), .in5(1'b0), .in6(1'b0), .in7(1'b0),
    .in8(1'b0), .in9(1'b0), .in10(1'b0), .in11(1'b0), .in12(1'b0), .in13(1'b0), .in14(1'b0), .in15(1'b0),
    .out(out_3[15]), .sel(in_2));
endmodule

module BEQ (
  input  [15:0] A,
  input  [15:0] B,
  output out_3
);

  wire [15:0] subtractor_1_out_3;

  Subtractor subtractor_1 (.in_1(A), .in_2(B), .out_3(subtractor_1_out_3));
  nor nor_1 (out_3, subtractor_1_out_3[0], subtractor_1_out_3[1], subtractor_1_out_3[2], subtractor_1_out_3[3], subtractor_1_out_3[4], subtractor_1_out_3[5], subtractor_1_out_3[6], subtractor_1_out_3[7], subtractor_1_out_3[8], subtractor_1_out_3[9], subtractor_1_out_3[10], subtractor_1_out_3[11], subtractor_1_out_3[12], subtractor_1_out_3[13], subtractor_1_out_3[14], subtractor_1_out_3[15]);
endmodule

module SLT (
  input  [15:0] A,
  input  [15:0] B,
  output out_3
);

  wire beq_1_out_3;
  wire [15:0] subtractor_1_out_3;

  Subtractor subtractor_1 (.in_1(A), .in_2(B), .out_3(subtractor_1_out_3));
  BEQ beq_1 (.A(A), .B(B), .out_3(beq_1_out_3));
  nor nor_1 (out_3, subtractor_1_out_3[15], beq_1_out_3);
endmodule

module Carry_Look_Ahead (
  input  Cin,
  input  [3:0] in_2,
  input  [3:0] in_3,
  output out_4,
  output C1,
  output C2,
  output C3
);

  wire and_1_out, and_2_out, and_3_out, and_4_out, and_5_out, and_6_out, and_7_out, and_8_out, and_9_out,
       and_10_out, and_11_out, and_12_out, and_13_out, and_14_out, and_15_out, and_16_out, and_17_out,
       and_18_out, and_19_out, and_20_out, and_21_out, and_22_out, and_23_out, and_24_out, and_25_out,
       and_26_out, and_27_out, and_28_out, or_4_out, or_5_out;

  and and_1 (and_1_out, in_2[2], in_3[2]);
  and and_2 (and_2_out, in_3[2], and_19_out);
  and and_3 (and_3_out, in_3[2], and_20_out);
  and and_4 (and_4_out, in_3[2], and_21_out);
  and and_5 (and_5_out, in_2[2], and_19_out);
  and and_6 (and_6_out, in_2[2], and_20_out);
  and and_7 (and_7_out, in_2[2], and_21_out);
  and and_8 (and_8_out, in_2[3], in_3[3]);
  and and_9 (and_9_out, in_3[3], and_1_out);
  and and_10 (and_10_out, in_3[3], and_2_out);
  and and_11 (and_11_out, in_3[3], and_3_out);
  and and_12 (and_12_out, in_3[3], and_4_out);
  and and_13 (and_13_out, in_3[3], and_5_out);
  buf and_14 (and_14_out, in_3[3]);  // AND_Gate
  and and_15 (and_15_out, in_3[3], and_7_out);
  and and_16 (and_16_out, in_2[0], in_3[0]);
  and and_17 (and_17_out, in_3[0], Cin);
  and and_18 (and_18_out, Cin, in_2[0]);
  and and_19 (and_19_out, in_2[1], in_3[1]);
  and and_20 (and_20_out, in_3[1], out_4);
  and and_21 (and_21_out, out_4, in_2[1]);
  or or_1 (out_4, and_16_out, and_17_out, and_18_out);
  or or_2 (C1, and_19_out, and_20_out, and_21_out);
  or or_3 (C2, and_1_out, and_2_out, and_3_out, and_4_out, and_5_out, and_6_out, and_7_out);
  and and_22 (and_22_out, and_1_out, in_2[3]);
  and and_23 (and_23_out, and_2_out, in_2[3]);
  and and_24 (and_24_out, and_3_out, in_2[3]);
  and and_25 (and_25_out, and_4_out, in_2[3]);
  and and_26 (and_26_out, and_5_out, in_2[3]);
  and and_27 (and_27_out, and_6_out, in_2[3]);
  and and_28 (and_28_out, and_7_out, in_2[3]);
  or or_4 (or_4_out, and_8_out, and_9_out, and_10_out, and_11_out, and_12_out, and_13_out, and_14_out, and_15_out);
  or or_5 (or_5_out, and_22_out, and_23_out, and_24_out, and_25_out, and_26_out, and_27_out, and_28_out);
  or or_6 (C3, or_4_out, or_5_out);
endmodule

module Control_Unit (
  input  [3:0] in_1,
  output RegWrite,
  output ALUsrc,
  output MemToReg,
  output MemRead,
  output MemWrite,
  output Branch,
  output RegDst
);

  wire ADD_out, ADDi_out, AND_out, ANDi_out, J_out, NOR_out, OR_out, ORi_out, SLL_out, SLT_out, SRL_out,
       SUB_out;

  and ADD (ADD_out, ~in_1[3], ~in_1[2], ~in_1[1], ~in_1[0]);  // AND_Gate
  and SUB (SUB_out, ~in_1[3], ~in_1[2], ~in_1[1], in_1[0]);  // AND_Gate
  and AND (AND_out, ~in_1[3], ~in_1[2], in_1[1], ~in_1[0]);  // AND_Gate
  and OR (OR_out, ~in_1[3], ~in_1[2], in_1[1], in_1[0]);  // AND_Gate
  and NOR (NOR_out, ~in_1[3], in_1[2], ~in_1[1], ~in_1[0]);  // AND_Gate
  and SLL (SLL_out, ~in_1[3], in_1[2], ~in_1[1], in_1[0]);  // AND_Gate
  and SRL (SRL_out, ~in_1[3], in_1[2], in_1[1], ~in_1[0]);  // AND_Gate
  and SLT (SLT_out, ~in_1[3], in_1[2], in_1[1], in_1[0]);  // AND_Gate
  and ORi (ORi_out, in_1[3], ~in_1[2], ~in_1[1], in_1[0]);  // AND_Gate
  and ANDi (ANDi_out, in_1[3], ~in_1[2], ~in_1[1], ~in_1[0]);  // AND_Gate
  and ADDi (ADDi_out, in_1[3], ~in_1[2], in_1[1], ~in_1[0]);  // AND_Gate
  and LW (MemRead, in_1[3], ~in_1[2], in_1[1], in_1[0]);  // AND_Gate
  and SW (MemWrite, in_1[3], in_1[2], ~in_1[1], ~in_1[0]);  // AND_Gate
  and BEQ (Branch, in_1[3], in_1[2], ~in_1[1], in_1[0]);  // AND_Gate
  and J (J_out, in_1[3], in_1[2], in_1[1], ~in_1[0]);  // AND_Gate
  // AND_Gate Nop has open pins: in0=in_1[3], in1=in_1[2], in2=in_1[1], in3=in_1[0], out=open
  or or_2 (RegWrite, ADD_out, SUB_out, AND_out, OR_out, NOR_out, SLL_out, SRL_out, SLT_out, ANDi_out, ORi_out, ADDi_out, MemRead);
  or or_3 (ALUsrc, ANDi_out, ORi_out, ADDi_out, MemRead, MemWrite);
  or or_4 (RegDst, MemWrite, Branch);

  assign MemToReg = MemRead;
endmodule

module ALU (
);

  Multiplexer #(.select(4), .width(16)) multiplexer_1 ();  // open: in0, in1, in2, in3, in4, in5, in6, in7, in8, in9, in10, in11, in12, in13, in14, in15, out, sel, en
endmodule
