// Logisim project project332.circ as structural Verilog: 8 circuits, main circuit main
module main (
  input  in_1,
  output out_2,
  output Overhlow,
  output Carryout
);

  wire ALUSrc, and_1_out, Clk_out, control_unit_1_branch, MemRead, MemToReg, MemWrite, RegDst, RegWrite;
  wire [1:0] alu_control_1_operation, control_unit_1_aluop;
  wire [2:2] alu_control_1_operation_2;
  wire [3:0] multiplexer_1_out;
  wire [15:0] bit_extender_1_out, multiplexer_2_out, multiplexer_4_out, n16_bit_alu_1_result, ram_1_data,
       reg16_1_read_data_1, reg16_1_read_data_2;
  wire [19:0] adder_1_out, adder_2_out, bit_extender_2_out, multiplexer_3_out, register_1_q, rom_1_data;

  Register #(.width(20)) register_1 (.D(multiplexer_3_out), .Q(register_1_q), .clk(Clk_out), .clr(in_1));  // open: en
  Clock Clk (.out(Clk_out));
  Adder #(.width(20)) adder_1 (.a(20'h1), .b(register_1_q), .out(adder_1_out));  // open: cin, cout
  ROM #(.addrWidth(20), .dataWidth(20)) rom_1 (.addr(register_1_q), .data(rom_1_data));  // open: sel
  control_unit control_unit_1 (
    .Instruction_Last_4bits(rom_1_data[19:16]), .RegDst(RegDst), .AluSrc(ALUSrc), .MemToReg(MemToReg),
    .RegWrite(RegWrite), .MemRead(MemRead), .MemWrite(MemWrite), .ALUOp(control_unit_1_aluop),
    .Branch(control_unit_1_branch));
  Multiplexer #(.width(4)) multiplexer_1 (
    .in0(rom_1_data[11:8]), .in1(rom_1_data[7:4]), .out(multiplexer_1_out), .sel(RegDst));  // open: en
  reg16 reg16_1 (
    .data_in(multiplexer_4_out), .read_data_1(reg16_1_read_data_1), .read_reg_1(rom_1_data[15:12]),
    .read_data_2(reg16_1_read_data_2), .read_reg_2(rom_1_data[11:8]), .in_1(RegWrite),
    .in_3(multiplexer_1_out), .Clk(Clk_out));
  assign bit_extender_1_out = {{8{rom_1_data[7]}}, rom_1_data[7:0]};  // Bit_Extender bit_extender_1
  ALU_Control alu_control_1 (
    .ALUOp(control_unit_1_aluop), .Function(rom_1_data[19:16]),
    .Operation({alu_control_1_operation_2[2], alu_control_1_operation}));
  _16_bit_ALU u_16_bit_alu_1 (
    .operation(alu_control_1_operation), .Binvert(alu_control_1_operation_2[2]), .Zero(out_2),
    .Overflow(Overhlow), .Carry_Out(Carryout), .B(reg16_1_read_data_1), .A(multiplexer_2_out),
    .Result(n16_bit_alu_1_result));  // open: Carry_in
  Multiplexer #(.width(16)) multiplexer_2 (
    .in0(reg16_1_read_data_2), .in1(bit_extender_1_out), .out(multiplexer_2_out), .sel(ALUSrc));  // open: en
  and and_1 (and_1_out, control_unit_1_branch, out_2);
  Adder #(.width(20)) adder_2 (.a(adder_1_out), .b(bit_extender_2_out), .out(adder_2_out));  // open: cin, cout
  Multiplexer #(.width(20)) multiplexer_3 (
    .in0(adder_1_out), .in1(adder_2_out), .out(multiplexer_3_out), .sel(and_1_out));  // open: en
  Multiplexer #(.width(16)) multiplexer_4 (
    .in0(n16_bit_alu_1_result), .in1(ram_1_data), .out(multiplexer_4_out), .sel(MemToReg));  // open: en
  RAM #(.addrWidth(16), .dataWidth(16), .bus("separate")) ram_1 (
    .addr(n16_bit_alu_1_result), .din(reg16_1_read_data_2), .data(ram_1_data), .str(MemWrite), .clk(Clk_out),
    .ld(MemRead));  // open: sel, clr
  assign bit_extender_2_out = {{4{bit_extender_1_out[15]}}, bit_extender_1_out};  // Bit_Extender bit_extender_2

  // Notes on the sheet:
  //   contents of rom_1 (hex, n*v repeats v):
  //   1230 30f04 1f30 11000 10000
endmodule

// Reg
module reg16 (
  input  in_1,
  input  [15:0] data_in,
  input  [3:0] in_3,
  input  [3:0] read_reg_1,
  input  [3:0] read_reg_2,
  input  Clk,
  output [15:0] read_data_1,
  output [15:0] read_data_2
);

  wire and_1_out, and_2_out, and_3_out, and_4_out, and_5_out, and_6_out, and_7_out, and_8_out, and_9_out,
       and_10_out, and_11_out, and_12_out, and_13_out, and_14_out, and_15_out, and_16_out, decoder_1_out0,
       decoder_1_out1, decoder_1_out2, decoder_1_out3, decoder_1_out4, decoder_1_out5, decoder_1_out6,
       decoder_1_out7, decoder_1_out8, decoder_1_out9, decoder_1_out10, decoder_1_out11, decoder_1_out12,
       decoder_1_out13, decoder_1_out14, decoder_1_out15;
  wire [15:0] register_1_q, register_2_q, register_3_q, register_4_q, register_5_q, register_6_q,
       register_7_q, register_8_q, register_9_q, register_10_q, register_11_q, register_12_q, register_13_q,
       register_14_q, register_15_q, register_16_q;

  Decoder #(.select(4)) decoder_1 (
    .out0(decoder_1_out0), .out1(decoder_1_out1), .out2(decoder_1_out2), .out3(decoder_1_out3),
    .out4(decoder_1_out4), .out5(decoder_1_out5), .out6(decoder_1_out6), .out7(decoder_1_out7),
    .out8(decoder_1_out8), .out9(decoder_1_out9), .out10(decoder_1_out10), .out11(decoder_1_out11),
    .out12(decoder_1_out12), .out13(decoder_1_out13), .out14(decoder_1_out14), .out15(decoder_1_out15),
    .sel(in_3));  // open: en
  and and_1 (and_1_out, in_1, decoder_1_out0);
  and and_2 (and_2_out, in_1, decoder_1_out1);
  and and_3 (and_3_out, in_1, decoder_1_out2);
  and and_4 (and_4_out, in_1, decoder_1_out3);
  and and_5 (and_5_out, in_1, decoder_1_out4);
  and and_6 (and_6_out, in_1, decoder_1_out5);
  and and_7 (and_7_out, in_1, decoder_1_out6);
  and and_8 (and_8_out, in_1, decoder_1_out7);
  Register #(.width(16)) register_1 (.D(data_in), .en(and_1_out), .Q(register_1_q), .clk(Clk));  // open: clr
  Register #(.width(16)) register_2 (.D(data_in), .en(and_2_out), .Q(register_2_q), .clk(Clk));  // open: clr
  Register #(.width(16)) register_3 (.D(data_in), .en(and_3_out), .Q(register_3_q), .clk(Clk));  // open: clr
  Register #(.width(16)) register_4 (.D(data_in), .en(and_4_out), .Q(register_4_q), .clk(Clk));  // open: clr
  Register #(.width(16)) register_5 (.D(data_in), .en(and_5_out), .Q(register_5_q), .clk(Clk));  // open: clr
  Register #(.width(16)) register_6 (.D(data_in), .en(and_6_out), .Q(register_6_q), .clk(Clk));  // open: clr
  Register #(.width(16)) register_7 (.D(data_in), .en(and_7_out), .Q(register_7_q), .clk(Clk));  // open: clr
  Register #(.width(16)) register_8 (.D(data_in), .en(and_8_out), .Q(register_8_q), .clk(Clk));  // open: clr
  and and_9 (and_9_out, in_1, decoder_1_out8);
  and and_10 (and_10_out, in_1, decoder_1_out9);
  and and_11 (and_11_out, in_1, decoder_1_out10);
  and and_12 (and_12_out, in_1, decoder_1_out11);
  and and_13 (and_13_out, in_1, decoder_1_out12);
  and and_14 (and_14_out, in_1, decoder_1_out13);
  and and_15 (and_15_out, in_1, decoder_1_out14);
  and and_16 (and_16_out, in_1, decoder_1_out15);
  Register #(.width(16)) register_9 (.D(data_in), .en(and_9_out), .Q(register_9_q), .clk(Clk));  // open: clr
  Register #(.width(16)) register_10 (.D(data_in), .en(and_10_out), .Q(register_10_q), .clk(Clk));  // open: clr
  Register #(.width(16)) register_11 (.D(data_in), .en(and_11_out), .Q(register_11_q), .clk(Clk));  // open: clr
  Register #(.width(16)) register_12 (.D(data_in), .en(and_12_out), .Q(register_12_q), .clk(Clk));  // open: clr
  Register #(.width(16)) register_13 (.D(data_in), .en(and_13_out), .Q(register_13_q), .clk(Clk));  // open: clr
  Register #(.width(16)) register_14 (.D(data_in), .en(and_14_out), .Q(register_14_q), .clk(Clk));  // open: clr
  Register #(.width(16)) register_15 (.D(data_in), .en(and_15_out), .Q(register_15_q), .clk(Clk));  // open: clr
  Register #(.width(16)) register_16 (.D(data_in), .en(and_16_out), .Q(register_16_q), .clk(Clk));  // open: clr
  Multiplexer #(.select(4), .width(16)) multiplexer_1 (
    .in0(register_1_q), .in1(register_2_q), .in2(register_3_q), .in3(register_4_q), .in4(register_5_q),
    .in5(register_6_q), .in6(register_7_q), .in7(register_8_q), .in8(register_9_q), .in9(register_10_q),
    .in10(register_11_q), .in11(register_12_q), .in12(register_13_q), .in13(register_14_q),
    .in14(register_15_q), .in15(register_16_q), .out(read_data_1), .sel(read_reg_1));  // open: en
  Multiplexer #(.select(4), .width(16)) multiplexer_2 (
    .in0(register_1_q), .in1(register_2_q), .in2(register_3_q), .in3(register_4_q), .in4(register_5_q),
    .in5(register_6_q), .in6(register_7_q), .in7(register_8_q), .in8(register_9_q), .in9(register_10_q),
    .in10(register_11_q), .in11(register_12_q), .in12(register_13_q), .in13(register_14_q),
    .in14(register_15_q), .in15(register_16_q), .out(read_data_2), .sel(read_reg_2));  // open: en
endmodule

// ALU
module _16_bit_ALU (
  input  Carry_in,
  input  [15:0] B,
  input  [15:0] A,
  input  [1:0] operation,
  input  Binvert,
  output Zero,
  output [15:0] Result,
  output Overflow,
  output Carry_Out
);

  wire n1_bit_alu_1_out_7, n1_bit_alu_2_out_7, n1_bit_alu_3_out_7, n1_bit_alu_4_out_7, n1_bit_alu_5_out_7,
       n1_bit_alu_6_out_7, n1_bit_alu_7_out_7, n1_bit_alu_8_out_7, n1_bit_alu_9_out_7, n1_bit_alu_10_out_7,
       n1_bit_alu_11_out_7, n1_bit_alu_12_out_7, n1_bit_alu_13_out_7, n1_bit_alu_14_out_7;

  _1_bit_ALU u_1_bit_alu_1 (
    .A(A[0]), .B(B[0]), .Carry_In(Carry_in), .Binvert(Binvert), .Operation(operation), .Result_O(Result[0]),
    .out_7(n1_bit_alu_1_out_7));
  _1_bit_ALU u_1_bit_alu_2 (
    .A(A[1]), .B(B[1]), .Carry_In(n1_bit_alu_1_out_7), .Binvert(Binvert), .Operation(operation),
    .Result_O(Result[1]), .out_7(n1_bit_alu_2_out_7));
  _1_bit_ALU u_1_bit_alu_3 (
    .A(A[2]), .B(B[2]), .Carry_In(n1_bit_alu_2_out_7), .Binvert(Binvert), .Operation(operation),
    .Result_O(Result[2]), .out_7(n1_bit_alu_3_out_7));
  _1_bit_ALU u_1_bit_alu_4 (
    .A(A[3]), .B(B[3]), .Carry_In(n1_bit_alu_3_out_7), .Binvert(Binvert), .Operation(operation),
    .Result_O(Result[3]), .out_7(n1_bit_alu_4_out_7));
  _1_bit_ALU u_1_bit_alu_5 (
    .A(A[4]), .B(B[4]), .Carry_In(n1_bit_alu_4_out_7), .Binvert(Binvert), .Operation(operation),
    .Result_O(Result[4]), .out_7(n1_bit_alu_5_out_7));
  _1_bit_ALU u_1_bit_alu_6 (
    .A(A[5]), .B(B[5]), .Carry_In(n1_bit_alu_5_out_7), .Binvert(Binvert), .Operation(operation),
    .Result_O(Result[5]), .out_7(n1_bit_alu_6_out_7));
  _1_bit_ALU u_1_bit_alu_7 (
    .A(A[6]), .B(B[6]), .Carry_In(n1_bit_alu_6_out_7), .Binvert(Binvert), .Operation(operation),
    .Result_O(Result[6]), .out_7(n1_bit_alu_7_out_7));
  _1_bit_ALU u_1_bit_alu_8 (
    .A(A[7]), .B(B[7]), .Carry_In(n1_bit_alu_7_out_7), .Binvert(Binvert), .Operation(operation),
    .Result_O(Result[7]), .out_7(n1_bit_alu_8_out_7));
  _1_bit_ALU u_1_bit_alu_9 (
    .A(A[8]), .B(B[8]), .Carry_In(n1_bit_alu_8_out_7), .Binvert(Binvert), .Operation(operation),
    .Result_O(Result[8]), .out_7(n1_bit_alu_9_out_7));
  _1_bit_ALU u_1_bit_alu_10 (
    .A(A[8]), .B(B[8]), .Carry_In(n1_bit_alu_9_out_7), .Binvert(Binvert), .Operation(operation),
    .Result_O(Result[9]), .out_7(n1_bit_alu_10_out_7));
  _1_bit_ALU u_1_bit_alu_11 (
    .A(A[8]), .B(B[8]), .Carry_In(n1_bit_alu_10_out_7), .Binvert(Binvert), .Operation(operation),
    .Result_O(Result[10]), .out_7(n1_bit_alu_11_out_7));
  _1_bit_ALU u_1_bit_alu_12 (
    .A(A[8]), .B(B[8]), .Carry_In(n1_bit_alu_11_out_7), .Binvert(Binvert), .Operation(operation),
    .Result_O(Result[11]), .out_7(n1_bit_alu_12_out_7));
  _1_bit_ALU u_1_bit_alu_13 (
    .A(A[8]), .B(B[8]), .Carry_In(n1_bit_alu_12_out_7), .Binvert(Binvert), .Operation(operation),
    .Result_O(Result[12]), .out_7(n1_bit_alu_13_out_7));
  _1_bit_ALU u_1_bit_alu_14 (
    .A(A[8]), .B(B[8]), .Carry_In(n1_bit_alu_13_out_7), .Binvert(Binvert), .Operation(operation),
    .Result_O(Result[13]), .out_7(n1_bit_alu_14_out_7));
  _1_bit_ALU u_1_bit_alu_15 (
    .A(A[8]), .B(B[8]), .Carry_In(n1_bit_alu_14_out_7), .Binvert(Binvert), .Operation(operation),
    .Result_O(Result[14]), .out_7(Result[7]));
  _1_bit_ALU u_1_bit_alu_16 (
    .A(A[8]), .B(B[8]), .Carry_In(Result[7]), .Binvert(Binvert), .Operation(operation),
    .Result_O(Result[15]), .out_7(Carry_Out));
  nor nor_1 (Zero, Result[0], Result[1], Result[2], Result[3], Result[4], Result[5], Result[6], Result[7], Result[8], Result[9], Result[10], Result[11], Result[12], Result[13], Result[14], Result[15]);
  xor xor_1 (Overflow, Result[7], Carry_Out);

  // Other names for the same wires on the sheet: c15 = Carry_Out; c14 = Result[7]
endmodule

module _1_bit_ALU (
  input  Carry_In,
  input  A,
  input  B,
  input  [1:0] Operation,
  input  Binvert,
  output Result_O,
  output out_7
);

  wire adder_1_out, and_1_out, buffer_1_out, multiplexer_1_out, or_1_out, subtractor_1_out;

  buf buffer_1 (buffer_1_out, B);
  Multiplexer #(.enable("false")) multiplexer_1 (.in0(B), .in1(buffer_1_out), .out(multiplexer_1_out), .sel(Binvert));
  Subtractor #(.width(1)) subtractor_1 (.a(A), .b(B), .out(subtractor_1_out));  // open: bin, bout
  and and_1 (and_1_out, A, B);
  or or_1 (or_1_out, A, B);
  Adder #(.width(1)) adder_1 (.a(A), .b(multiplexer_1_out), .out(adder_1_out), .cin(Carry_In), .cout(out_7));
  Multiplexer #(.select(2), .enable("false")) multiplexer_2 (
    .in0(and_1_out), .in1(or_1_out), .in2(adder_1_out), .in3(subtractor_1_out), .out(Result_O),
    .sel(Operation));
endmodule

module single_datapath (
  input  [19:0] in_1,
  input  in_2,
  input  [15:0] in_3,
  input  [15:0] in_4,
  input  MemWrite,
  input  MemRead,
  output [15:0] out_7
);

  wire clock_1_out, clock_2_out;
  wire [19:0] adder_1_out, register_1_q;

  Register #(.width(20)) register_1 (.D(adder_1_out), .Q(register_1_q), .clk(clock_1_out), .clr(in_2));  // open: en
  Clock clock_1 (.out(clock_1_out));
  Adder #(.width(20)) adder_1 (.a(20'h1), .b(register_1_q), .out(adder_1_out));  // open: cin, cout
  ROM #(.addrWidth(20), .dataWidth(20)) rom_1 (.addr(register_1_q), .data(in_1));  // open: sel
  Clock clock_2 (.out(clock_2_out));
  RAM #(.addrWidth(16), .dataWidth(16), .bus("separate")) ram_1 (
    .addr(in_3), .din(in_4), .data(out_7), .str(MemWrite), .clk(clock_2_out), .ld(MemRead));  // open: sel, clr
endmodule

// Ctrl Unit
module control_unit (
  input  [3:0] Instruction_Last_4bits,
  output RegDst,
  output AluSrc,
  output MemToReg,
  output RegWrite,
  output MemRead,
  output MemWrite,
  output Branch,
  output [1:0] ALUOp
);

  and R_format (ALUOp[1], ~Instruction_Last_4bits[0], ~Instruction_Last_4bits[1], ~Instruction_Last_4bits[2], ~Instruction_Last_4bits[3]);  // AND_Gate
  and lw (MemRead, Instruction_Last_4bits[0], Instruction_Last_4bits[1], ~Instruction_Last_4bits[2], ~Instruction_Last_4bits[3]);  // AND_Gate
  and sw (MemWrite, Instruction_Last_4bits[0], ~Instruction_Last_4bits[1], Instruction_Last_4bits[2], Instruction_Last_4bits[3]);  // AND_Gate
  and Beq (ALUOp[0], ~Instruction_Last_4bits[0], Instruction_Last_4bits[1], ~Instruction_Last_4bits[2], ~Instruction_Last_4bits[3]);  // AND_Gate
  or or_1 (AluSrc, MemRead, MemWrite);
  or or_2 (RegWrite, ALUOp[1], MemRead);

  assign Branch = ALUOp[0];
  assign MemToReg = MemRead;
  assign RegDst = ALUOp[1];
endmodule

// ALU Ctrl
module ALU_Control (
  input  [1:0] ALUOp,
  input  [3:0] Function,
  output [2:0] Operation
);

  wire and_1_out, and_2_out, not_1_out, not_2_out, not_3_out, not_4_out;

  not not_1 (not_1_out, ALUOp[0]);
  not not_2 (not_2_out, ALUOp[1]);
  not not_3 (not_3_out, Function[0]);
  not not_4 (not_4_out, Function[2]);
  and and_1 (and_1_out, ALUOp[1], not_4_out);
  and and_2 (and_2_out, ALUOp[1], Function[1]);
  or S0 (Operation[0], ALUOp[1], Function[0]);
  or S1 (Operation[1], and_1_out, not_2_out, not_1_out, and_2_out);
  or S2 (Operation[2], ALUOp[1], Function[1]);
endmodule

module sub (
  input  [1:0] in_1,
  input  in_2,
  input  [15:0] in_3,
  input  [15:0] in_4,
  output [15:0] out_5
);

  _16_bit_ALU u_16_bit_alu_1 (
    .operation(in_1), .Binvert(in_2), .B(in_3), .A(in_4), .Result(out_5));  // open: Carry_in, Zero, Overflow, Carry_Out
endmodule
