// Logisim project SARHAN.circ as structural Verilog: 5 circuits, main circuit main
module main (
  input  [3:0] RS,
  input  [3:0] RT,
  input  [3:0] RD,
  input  in_4,
  input  REGWRITE,
  output out_6,
  output [15:0] out_7,
  output out_8,
  output out_9
);

  wire CLK_out, control_unit_1_branch, control_unit_1_memread, control_unit_1_memtoreg,
       control_unit_1_memwrite, control_unit_1_regdst, control_unit_1_regwrite, undriven_2;
  wire [1:0] control_unit_1_aluop;
  wire [3:0] multiplexer_2_out, undriven;
  wire [7:0] adder_2_out;
  wire [15:0] adder_1_out, bit_extender_1_out, multiplexer_1_out, multiplexer_3_out,
       n16_bit_alu_1_alu_output, n16bit_1_read_data_1, n16bit_1_read_data_2, PC_q, ram_1_data;
  wire [15:12] rom_1_data;

  Multiplexer multiplexer_1 (.in0(adder_2_out[0]), .in1(PC_q[0]), .out(multiplexer_1_out[0]));  // open: sel, en
  Register #(.width(16)) PC (.D(multiplexer_1_out), .Q(PC_q), .clk(CLK_out), .clr(in_4));  // open: en
  Clock CLK (.out(CLK_out));
  Adder #(.width(16)) adder_1 (.a(PC_q), .b(16'h1), .out(adder_1_out));  // open: cin, cout
  CONTROL_UNIT control_unit_1 (
    .Instruction_Last_4bits(undriven), .RegDst(control_unit_1_regdst), .MemToReg(control_unit_1_memtoreg),
    .RegWrite(control_unit_1_regwrite), .MemRead(control_unit_1_memread), .MemWrite(control_unit_1_memwrite),
    .Branch(control_unit_1_branch), .ALUOp(control_unit_1_aluop));  // open: AluSrc
  ROM #(.addrWidth(16), .dataWidth(16)) rom_1 (
    .addr(PC_q), .data({rom_1_data, RS[2:0], RT[2:0], RD[2:0], undriven[2:0]}));  // open: sel
  Multiplexer #(.width(4)) multiplexer_2 (
    .in0(RT), .in1(RD), .out(multiplexer_2_out), .sel(control_unit_1_regdst));  // open: en
  _16BIT u_16bit_1 (
    .Write_Data(out_7), .Read_Data_1(n16bit_1_read_data_1), .Read_Register_1(RS),
    .Read_Data_2(n16bit_1_read_data_2), .Read_Register_2(RT), .RegWrite(REGWRITE),
    .CLK(control_unit_1_regwrite), .Write_Register(multiplexer_2_out));
  assign bit_extender_1_out = {{12{1'b0}}, rom_1_data};  // Bit_Extender bit_extender_1
  Adder adder_2 (.a(adder_1_out[7:0]), .b(bit_extender_1_out[7:0]), .out(adder_2_out));  // open: cin, cout
  Multiplexer #(.width(16)) multiplexer_3 (
    .in0(n16bit_1_read_data_2), .in1(bit_extender_1_out), .out(multiplexer_3_out), .sel(control_unit_1_branch));  // open: en
  _16_BIT_ALU u_16_bit_alu_1 (
    .A(n16bit_1_read_data_1), .B(multiplexer_3_out), .Zero_Flag(out_6),
    .ALU_Output(n16_bit_alu_1_alu_output), .Overflow_Flag(out_8), .C_Out(out_9), .B_Invert(undriven_2),
    .ALU_Op(control_unit_1_aluop));
  RAM #(.addrWidth(16), .dataWidth(16), .bus("separate")) ram_1 (
    .addr(n16_bit_alu_1_alu_output), .data(ram_1_data), .str(control_unit_1_memwrite),
    .ld(control_unit_1_memread));  // open: din, sel, clk, clr
  Multiplexer #(.width(16)) multiplexer_4 (
    .in0(n16_bit_alu_1_alu_output), .in1(ram_1_data), .out(out_7), .sel(control_unit_1_memtoreg));  // open: en
  // Pins of 3 and 4 bits meet at RD
  // Pins of 3 and 4 bits meet at RS
  // Pins of 1 and 16 bits meet at PC_q
  // Pins of 8 and 16 bits meet at adder_1_out
  // Pins of 8 and 16 bits meet at bit_extender_1_out
  // Pins of 3 and 4 bits meet at RT
  // Pins of 3 and 4 bits meet at undriven
  // Pins of 1 and 8 bits meet at adder_2_out
  // Pins of 1 and 16 bits meet at multiplexer_1_out
endmodule

module _16BIT (
  input  RegWrite,
  input  CLK,
  input  [15:0] Write_Data,
  input  [3:0] Read_Register_1,
  input  [3:0] Write_Register,
  input  [3:0] Read_Register_2,
  output [15:0] Read_Data_1,
  output [15:0] Read_Data_2
);

  wire and_1_out, and_2_out, and_3_out, and_4_out, and_5_out, and_6_out, and_7_out, and_8_out, and_9_out,
       and_10_out, and_11_out, and_12_out, and_13_out, and_14_out, and_15_out, and_16_out, decoder_1_out0,
       decoder_1_out1, decoder_1_out2, decoder_1_out3, decoder_1_out4, decoder_1_out5, decoder_1_out6,
       decoder_1_out7, decoder_1_out8, decoder_1_out9, decoder_1_out10, decoder_1_out11, decoder_1_out12,
       decoder_1_out13, decoder_1_out14, decoder_1_out15;
  wire [15:0] _0_q, _1_q, _2_q, _3_q, _4_q, _5_q, _6_q, _7_q, _8_q, _9_q, _10_q, _11_q, _12_q, _13_q, _14_q,
       _15_q;

  Decoder #(.select(4), .enable("false")) decoder_1 (
    .out0(decoder_1_out0), .out1(decoder_1_out1), .out2(decoder_1_out2), .out3(decoder_1_out3),
    .out4(decoder_1_out4), .out5(decoder_1_out5), .out6(decoder_1_out6), .out7(decoder_1_out7),
    .out8(decoder_1_out8), .out9(decoder_1_out9), .out10(decoder_1_out10), .out11(decoder_1_out11),
    .out12(decoder_1_out12), .out13(decoder_1_out13), .out14(decoder_1_out14), .out15(decoder_1_out15),
    .sel(Write_Register));
  and and_1 (and_1_out, decoder_1_out0, RegWrite);
  and and_2 (and_2_out, decoder_1_out1, RegWrite);
  and and_3 (and_3_out, decoder_1_out2, RegWrite);
  and and_4 (and_4_out, decoder_1_out3, RegWrite);
  and and_5 (and_5_out, decoder_1_out4, RegWrite);
  and and_6 (and_6_out, decoder_1_out5, RegWrite);
  and and_7 (and_7_out, decoder_1_out6, RegWrite);
  and and_8 (and_8_out, decoder_1_out7, RegWrite);
  and and_9 (and_9_out, decoder_1_out8, RegWrite);
  and and_10 (and_10_out, decoder_1_out9, RegWrite);
  and and_11 (and_11_out, decoder_1_out10, RegWrite);
  and and_12 (and_12_out, decoder_1_out11, RegWrite);
  and and_13 (and_13_out, decoder_1_out12, RegWrite);
  and and_14 (and_14_out, decoder_1_out13, RegWrite);
  and and_15 (and_15_out, decoder_1_out14, RegWrite);
  and and_16 (and_16_out, decoder_1_out15, RegWrite);
  Register #(.width(16)) _0 (.D(Write_Data), .en(and_1_out), .Q(_0_q), .clk(CLK));  // open: clr
  Register #(.width(16)) _1 (.D(Write_Data), .en(and_2_out), .Q(_1_q), .clk(CLK));  // open: clr
  Register #(.width(16)) _2 (.D(Write_Data), .en(and_3_out), .Q(_2_q), .clk(CLK));  // open: clr
  Register #(.width(16)) _3 (.D(Write_Data), .en(and_4_out), .Q(_3_q), .clk(CLK));  // open: clr
  Register #(.width(16)) _4 (.D(Write_Data), .en(and_5_out), .Q(_4_q), .clk(CLK));  // open: clr
  Register #(.width(16)) _5 (.D(Write_Data), .en(and_6_out), .Q(_5_q), .clk(CLK));  // open: clr
  Register #(.width(16)) _6 (.D(Write_Data), .en(and_7_out), .Q(_6_q), .clk(CLK));  // open: clr
  Register #(.width(16)) _7 (.D(Write_Data), .en(and_8_out), .Q(_7_q), .clk(CLK));  // open: clr
  Register #(.width(16)) _8 (.D(Write_Data), .en(and_9_out), .Q(_8_q), .clk(CLK));  // open: clr
  Register #(.width(16)) _9 (.D(Write_Data), .en(and_10_out), .Q(_9_q), .clk(CLK));  // open: clr
  Register #(.width(16)) _10 (.D(Write_Data), .en(and_11_out), .Q(_10_q), .clk(CLK));  // open: clr
  Register #(.width(16)) _11 (.D(Write_Data), .en(and_12_out), .Q(_11_q), .clk(CLK));  // open: clr
  Register #(.width(16)) _12 (.D(Write_Data), .en(and_13_out), .Q(_12_q), .clk(CLK));  // open: clr
  Register #(.width(16)) _13 (.D(Write_Data), .en(and_14_out), .Q(_13_q), .clk(CLK));  // open: clr
  Register #(.width(16)) _14 (.D(Write_Data), .en(and_15_out), .Q(_14_q), .clk(CLK));  // open: clr
  Register #(.width(16)) _15 (.D(Write_Data), .en(and_16_out), .Q(_15_q), .clk(CLK));  // open: clr
  Multiplexer #(.select(4), .width(16), .enable("false")) multiplexer_1 (
    .in0(_0_q), .in1(_1_q), .in2(_2_q), .in3(_3_q), .in4(_4_q), .in5(_5_q), .in6(_6_q), .in7(_7_q),
    .in8(_8_q), .in9(_9_q), .in10(_10_q), .in11(_11_q), .in12(_12_q), .in13(_13_q), .in14(_14_q),
    .in15(_15_q), .out(Read_Data_1), .sel(Read_Register_1));
  Multiplexer #(.select(4), .width(16), .enable("false")) multiplexer_2 (
    .in0(_0_q), .in1(_1_q), .in2(_2_q), .in3(_3_q), .in4(_4_q), .in5(_5_q), .in6(_6_q), .in7(_7_q),
    .in8(_8_q), .in9(_9_q), .in10(_10_q), .in11(_11_q), .in12(_12_q), .in13(_13_q), .in14(_14_q),
    .in15(_15_q), .out(Read_Data_2), .sel(Read_Register_2));
endmodule

module _16_BIT_ALU (
  input  B_Invert,
  input  [15:0] A,
  input  [15:0] B,
  input  [1:0] ALU_Op,
  output Zero_Flag,
  output [15:0] ALU_Output,
  output Overflow_Flag,
  output C_Out
);

  wire n1_bit_alu_1_c_out, n1_bit_alu_2_c_out, n1_bit_alu_3_c_out, n1_bit_alu_4_c_out, n1_bit_alu_5_c_out,
       n1_bit_alu_6_c_out, n1_bit_alu_7_c_out, n1_bit_alu_8_c_out, n1_bit_alu_9_c_out, n1_bit_alu_10_c_out,
       n1_bit_alu_11_c_out, n1_bit_alu_12_c_out, n1_bit_alu_13_c_out, n1_bit_alu_14_c_out,
       n1_bit_alu_15_c_out, n1_bit_alu_16_set;

  _1_BIT_ALU u_1_bit_alu_1 (
    .C_in(B_Invert), .Less(n1_bit_alu_16_set), .ALU_Output(ALU_Output[0]), .C_out(n1_bit_alu_1_c_out),
    .in_1(B[0]), .in_2(A[0]), .B_Invert(B_Invert), .ALU_Op(ALU_Op));  // open: Set
  _1_BIT_ALU u_1_bit_alu_2 (
    .C_in(n1_bit_alu_1_c_out), .Less(1'b0), .ALU_Output(ALU_Output[1]), .C_out(n1_bit_alu_2_c_out),
    .in_1(B[1]), .in_2(A[1]), .B_Invert(B_Invert), .ALU_Op(ALU_Op));  // open: Set
  _1_BIT_ALU u_1_bit_alu_3 (
    .C_in(n1_bit_alu_2_c_out), .Less(1'b0), .ALU_Output(ALU_Output[2]), .C_out(n1_bit_alu_3_c_out),
    .in_1(B[2]), .in_2(A[2]), .B_Invert(B_Invert), .ALU_Op(ALU_Op));  // open: Set
  _1_BIT_ALU u_1_bit_alu_4 (
    .C_in(n1_bit_alu_3_c_out), .Less(1'b0), .ALU_Output(ALU_Output[3]), .C_out(n1_bit_alu_4_c_out),
    .in_1(B[3]), .in_2(A[3]), .B_Invert(B_Invert), .ALU_Op(ALU_Op));  // open: Set
  _1_BIT_ALU u_1_bit_alu_5 (
    .C_in(n1_bit_alu_4_c_out), .Less(1'b0), .ALU_Output(ALU_Output[4]), .C_out(n1_bit_alu_5_c_out),
    .in_1(B[4]), .in_2(A[4]), .B_Invert(B_Invert), .ALU_Op(ALU_Op));  // open: Set
  _1_BIT_ALU u_1_bit_alu_6 (
    .C_in(n1_bit_alu_5_c_out), .Less(1'b0), .ALU_Output(ALU_Output[5]), .C_out(n1_bit_alu_6_c_out),
    .in_1(B[5]), .in_2(A[5]), .B_Invert(B_Invert), .ALU_Op(ALU_Op));  // open: Set
  _1_BIT_ALU u_1_bit_alu_7 (
    .C_in(n1_bit_alu_6_c_out), .Less(1'b0), .ALU_Output(ALU_Output[6]), .C_out(n1_bit_alu_7_c_out),
    .in_1(B[6]), .in_2(A[6]), .B_Invert(B_Invert), .ALU_Op(ALU_Op));  // open: Set
  _1_BIT_ALU u_1_bit_alu_8 (
    .C_in(n1_bit_alu_7_c_out), .Less(1'b0), .ALU_Output(ALU_Output[7]), .C_out(n1_bit_alu_8_c_out),
    .in_1(B[7]), .in_2(A[7]), .B_Invert(B_Invert), .ALU_Op(ALU_Op));  // open: Set
  _1_BIT_ALU u_1_bit_alu_9 (
    .C_in(n1_bit_alu_8_c_out), .Less(1'b0), .ALU_Output(ALU_Output[8]), .C_out(n1_bit_alu_9_c_out),
    .in_1(B[8]), .in_2(A[8]), .B_Invert(B_Invert), .ALU_Op(ALU_Op));  // open: Set
  _1_BIT_ALU u_1_bit_alu_10 (
    .C_in(n1_bit_alu_9_c_out), .Less(1'b0), .ALU_Output(ALU_Output[9]), .C_out(n1_bit_alu_10_c_out),
    .in_1(B[9]), .in_2(A[9]), .B_Invert(B_Invert), .ALU_Op(ALU_Op));  // open: Set
  _1_BIT_ALU u_1_bit_alu_11 (
    .C_in(n1_bit_alu_10_c_out), .Less(1'b0), .ALU_Output(ALU_Output[10]), .C_out(n1_bit_alu_11_c_out),
    .in_1(B[10]), .in_2(A[10]), .B_Invert(B_Invert), .ALU_Op(ALU_Op));  // open: Set
  _1_BIT_ALU u_1_bit_alu_12 (
    .C_in(n1_bit_alu_11_c_out), .Less(1'b0), .ALU_Output(ALU_Output[11]), .C_out(n1_bit_alu_12_c_out),
    .in_1(B[11]), .in_2(A[11]), .B_Invert(B_Invert), .ALU_Op(ALU_Op));  // open: Set
  _1_BIT_ALU u_1_bit_alu_13 (
    .C_in(n1_bit_alu_12_c_out), .Less(1'b0), .ALU_Output(ALU_Output[12]), .C_out(n1_bit_alu_13_c_out),
    .in_1(B[12]), .in_2(A[12]), .B_Invert(B_Invert), .ALU_Op(ALU_Op));  // open: Set
  _1_BIT_ALU u_1_bit_alu_14 (
    .C_in(n1_bit_alu_13_c_out), .Less(1'b0), .ALU_Output(ALU_Output[13]), .C_out(n1_bit_alu_14_c_out),
    .in_1(B[13]), .in_2(A[13]), .B_Invert(B_Invert), .ALU_Op(ALU_Op));  // open: Set
  _1_BIT_ALU u_1_bit_alu_15 (
    .C_in(n1_bit_alu_14_c_out), .Less(1'b0), .ALU_Output(ALU_Output[14]), .C_out(n1_bit_alu_15_c_out),
    .in_1(B[14]), .in_2(A[14]), .B_Invert(B_Invert), .ALU_Op(ALU_Op));  // open: Set
  _1_BIT_ALU u_1_bit_alu_16 (
    .C_in(n1_bit_alu_15_c_out), .Less(1'b0), .ALU_Output(ALU_Output[15]), .Set(n1_bit_alu_16_set),
    .C_out(C_Out), .in_1(B[15]), .in_2(A[15]), .B_Invert(B_Invert), .ALU_Op(ALU_Op));
  xor xor_1 (Overflow_Flag, n1_bit_alu_15_c_out, C_Out);
  nor nor_1 (Zero_Flag, ALU_Output[0], ALU_Output[1], ALU_Output[2], ALU_Output[3], ALU_Output[4], ALU_Output[5], ALU_Output[6], ALU_Output[7], ALU_Output[8], ALU_Output[9], ALU_Output[10], ALU_Output[11], ALU_Output[12], ALU_Output[13], ALU_Output[14], ALU_Output[15]);

  // Notes on the sheet:
  //   C_In
  //   Set
endmodule

module _1_BIT_ALU (
  input  in_1,
  input  in_2,
  input  C_in,
  input  B_Invert,
  input  Less,
  input  [1:0] ALU_Op,
  output ALU_Output,
  output Set,
  output C_out
);

  wire and_1_out, multiplexer_1_out, not_1_out, or_1_out;

  not not_1 (not_1_out, in_1);
  Multiplexer #(.enable("false")) multiplexer_1 (.in0(in_1), .in1(not_1_out), .out(multiplexer_1_out), .sel(B_Invert));
  and and_1 (and_1_out, in_2, in_1);
  or or_1 (or_1_out, in_2, in_1);
  Adder #(.width(1)) adder_1 (.a(in_2), .b(multiplexer_1_out), .out(Set), .cin(C_in), .cout(C_out));
  Multiplexer #(.select(2), .enable("false")) multiplexer_2 (
    .in0(and_1_out), .in1(or_1_out), .in2(Set), .in3(Less), .out(ALU_Output), .sel(ALU_Op));
endmodule

module CONTROL_UNIT (
  input  [3:0] Instruction_Last_4bits,
  output RegDst,
  output AluSrc,
  output MemToReg,
  output RegWrite,
  output MemRead,
  output MemWrite,
  output Branch,
  output [1:0] ALUOp
);

  and R_format (ALUOp[1], ~Instruction_Last_4bits[0], ~Instruction_Last_4bits[1], ~Instruction_Last_4bits[2], ~Instruction_Last_4bits[3]);  // AND_Gate
  and lw (MemRead, Instruction_Last_4bits[0], Instruction_Last_4bits[1], ~Instruction_Last_4bits[2], ~Instruction_Last_4bits[3]);  // AND_Gate
  and sw (MemWrite, Instruction_Last_4bits[0], ~Instruction_Last_4bits[1], Instruction_Last_4bits[2], Instruction_Last_4bits[3]);  // AND_Gate
  and Beq (ALUOp[0], ~Instruction_Last_4bits[0], Instruction_Last_4bits[1], ~Instruction_Last_4bits[2], ~Instruction_Last_4bits[3]);  // AND_Gate
  or or_1 (AluSrc, MemRead, MemWrite);
  or or_2 (RegWrite, ALUOp[1], MemRead);

  assign Branch = ALUOp[0];
  assign MemToReg = MemRead;
  assign RegDst = ALUOp[1];
endmodule
